// Digital circuit Final_CEDT_2023_01.dig as structural Verilog
module Final_CEDT_2023_01 (
  input  reset,
  input  clk,
  output C,
  output B,
  output A
);

  wire and_1_out, and_2_out, and_3_out, and_4_out, and_5_out, and_6_out, multiplexer_1_out,
       multiplexer_2_out, multiplexer_3_out, not_1_out, not_2_out, not_3_out, or_1_out, or_2_out, or_3_out;

  not not_1 (not_1_out, C);
  not not_2 (not_2_out, B);
  not not_3 (not_3_out, A);
  and and_1 (and_1_out, not_3_out, B);
  and and_2 (and_2_out, A, C);
  and and_3 (and_3_out, A, not_1_out);
  and and_4 (and_4_out, not_3_out, B);
  and and_5 (and_5_out, not_2_out, not_1_out);
  and and_6 (and_6_out, B, C);
  or or_1 (or_1_out, and_1_out, and_2_out);
  or or_2 (or_2_out, and_3_out, and_4_out);
  or or_3 (or_3_out, and_5_out, and_6_out);
  Multiplexer multiplexer_1 (.sel(reset), .in_0(or_1_out), .in_1(1'b0), .out(multiplexer_1_out));
  Multiplexer multiplexer_2 (.sel(reset), .in_0(or_2_out), .in_1(1'b0), .out(multiplexer_2_out));
  Multiplexer multiplexer_3 (.sel(reset), .in_0(or_3_out), .in_1(1'b0), .out(multiplexer_3_out));
  D_FF d_ff_1 (.D(multiplexer_1_out), .C(clk), .Q(C));  // open: nQ
  D_FF d_ff_2 (.D(multiplexer_2_out), .C(clk), .Q(B));  // open: nQ
  D_FF d_ff_3 (.D(multiplexer_3_out), .C(clk), .Q(A));  // open: nQ
endmodule

/* Test case TestCase:
clk reset C B A
0 0 0 0 0 
0 1 0 0 0
1 1 0 0 0
0 0 0 0 0
1 0 0 0 1
0 0 0 0 1
1 0 0 1 1
0 0 0 1 1
1 0 0 1 0
0 0 0 1 0
1 0 1 1 0
0 0 1 1 0
1 0 1 1 1
0 0 1 1 1
1 0 1 0 1
0 0 1 0 1
1 0 1 0 0
0 0 1 0 0
1 0 0 0 0
0 0 0 0 0
1 0 0 0 1
0 0 0 0 1
1 0 0 1 1
0 0 0 1 1
1 0 0 1 0
0 0 0 1 0
1 0 1 1 0
0 0 1 1 0
1 0 1 1 1
0 0 1 1 1
1 0 1 0 1
0 0 1 0 1
1 0 1 0 0
0 0 1 0 0
*/
