// Digital circuit Final_CEDT_2023_02.dig as structural Verilog
module Final_CEDT_2023_02 (
  input  [15:0] A,
  input  \input ,
  input  clk,
  output [7:0] sqrt,
  output [31:0] product,
  output busy,
  output [15:0] low,
  output [15:0] high,
  output [15:0] mid
);

  wire Compare_2_eq, Compare_2_gt, Compare_2_lt, Compare_eq, Compare_lt, Hshift, Lshift, or_2_out;
  wire [15:0] Hshift_s, Lshift_s, multiplexer_1_out, multiplexer_2_out, multiplexer_3_out, multiplexer_4_out,
       Sum_s;
  wire [16:0] Half_q;
  wire [16:16] Sum_c_o;

  Comparator #(.Bits(16)) Compare (.a(low), .b(high), .eq(Compare_eq), .lt(Compare_lt));  // open: gt
  Mul #(.Bits(16)) X_2 (.a(mid), .b(mid), .mul(product));
  Add #(.Bits(16)) u_Lshift (.a(mid), .b(16'h1), .c_i(1'b0), .s(Lshift_s));  // open: c_o
  Sub #(.Bits(16)) u_Hshift (.a(mid), .b(16'h1), .c_i(1'b0), .s(Hshift_s));  // open: c_o
  Comparator #(.Signed("true"), .Bits(32)) Compare_2 (
    .a(product), .b({{16{1'b0}}, A}), .gt(Compare_2_gt), .eq(Compare_2_eq), .lt(Compare_2_lt));
  Multiplexer #(.Bits(16)) multiplexer_1 (.sel(Lshift), .in_0(low), .in_1(Lshift_s), .out(multiplexer_1_out));
  Multiplexer #(.Bits(16)) multiplexer_2 (.sel(Hshift), .in_0(high), .in_1(Hshift_s), .out(multiplexer_2_out));
  or or_1 (busy, Compare_eq, Compare_lt);
  or or_2 (or_2_out, Compare_2_eq, Compare_2_lt);
  Multiplexer #(.Bits(16)) multiplexer_3 (
    .sel(\input ), .in_0(multiplexer_1_out), .in_1(16'h1), .out(multiplexer_3_out));
  Multiplexer #(.Bits(16)) multiplexer_4 (.sel(\input ), .in_0(multiplexer_2_out), .in_1(A), .out(multiplexer_4_out));
  and and_1 (Hshift, busy, Compare_2_gt);
  and and_2 (Lshift, or_2_out, busy);
  Add #(.Bits(16)) Sum (.a(multiplexer_3_out), .b(multiplexer_4_out), .c_i(1'b0), .s(Sum_s), .c_o(Sum_c_o[16]));
  Div #(.Bits(17)) Half (.a({Sum_c_o[16], Sum_s}), .b(17'h2), .q(Half_q));  // open: r
  D_FF #(.Bits(16), .Default(1)) Memory (.D(multiplexer_3_out), .C(clk), .Q(low));  // open: nQ
  D_FF #(.Bits(16)) Memory_2 (.D(Half_q[15:0]), .C(clk), .Q(mid));  // open: nQ
  D_FF #(.Bits(16)) Memory_3 (.D(multiplexer_4_out), .C(clk), .Q(high));  // open: nQ

  assign sqrt = high[7:0];
endmodule

/* Test case TestCase1:
clk A input sqrt busy
0 0 0 0 0
1 0 0 0 0
0 0 0 0 0
1 0 0 0 0
0 0 1 X X
1 0 1 X X
loop(x,1000)
0 0 0 X X
1 0 0 X X
end loop
0 0 0 0 0
1 0 0 0 0
*/

/* Test case TestCase2:
clk A input sqrt busy
0 0 0 0 0
1 0 0 0 0
0 0 0 0 0
1 0 0 0 0
0 1 1 X X
1 1 1 X X
loop(x,1000)
0 1 0 X X
1 1 0 X X
end loop
0 0 0 1 0
1 0 0 1 0
*/

/* Test case TestCase3:
clk A input sqrt busy
0 0 0 0 0
1 0 0 0 0
0 0 0 0 0
1 0 0 0 0
0 4 1 X X
1 4 1 X X
loop(x,1000)
0 4 0 X X
1 4 0 X X
end loop
0 0 0 2 0
1 0 0 2 0
*/

/* Test case TestCase4:
clk A input sqrt busy
0 0 0 0 0
1 0 0 0 0
0 0 0 0 0
1 0 0 0 0
0 9 1 X X
1 9 1 X X
loop(x,1000)
0 9 0 X X
1 9 0 X X
end loop
0 0 0 3 0
1 0 0 3 0
*/

/* Test case TestCase5:
clk A input sqrt busy
0 0 0 0 0
1 0 0 0 0
0 0 0 0 0
1 0 0 0 0
0 8 1 X X
1 8 1 X X
loop(x,1000)
0 8 0 X X
1 8 0 X X
end loop
0 0 0 2 0
1 0 0 2 0
*/
