// Digital circuit Final_CEDT_2023_03.dig as structural Verilog
module Final_CEDT_2023_03 (
  input  [15:0] A,
  input  \input ,
  input  clk,
  input  reset,
  output [15:0] mean,
  output busy,
  output [31:0] sum,
  output [3:0] count
);

  wire d_ff_1_nq, d_ff_2_q, d_ff_3_q;
  wire [3:0] Count_s, Load_2_q, multiplexer_2_out;
  wire [31:0] Load_q, multiplexer_1_out, Sum_s;
  wire [31:16] Calculate_q;

  D_FF d_ff_1 (.D(\input ), .C(clk), .nQ(d_ff_1_nq));  // open: Q
  Add #(.Bits(32)) u_Sum (.a(sum), .b({{16{1'b0}}, A}), .c_i(1'b0), .s(Sum_s));  // open: c_o
  Add #(.Bits(4)) u_Count (.a(count), .b(4'b0001), .c_i(1'b0), .s(Count_s));  // open: c_o
  D_FF d_ff_2 (.D(\input ), .C(clk), .Q(d_ff_2_q));  // open: nQ
  D_FF d_ff_3 (.D(d_ff_1_nq), .C(clk), .Q(d_ff_3_q));  // open: nQ
  and and_1 (busy, d_ff_2_q, d_ff_3_q);
  D_FF #(.Bits(32)) Load (.D(Sum_s), .C(busy), .Q(Load_q));  // open: nQ
  D_FF #(.Bits(4)) Load_2 (.D(Count_s), .C(busy), .Q(Load_2_q));  // open: nQ
  Multiplexer #(.Bits(32)) multiplexer_1 (.sel(reset), .in_0(Load_q), .in_1({32{1'b0}}), .out(multiplexer_1_out));
  Multiplexer #(.Bits(4)) multiplexer_2 (.sel(reset), .in_0(Load_2_q), .in_1(4'b0000), .out(multiplexer_2_out));
  D_FF #(.Bits(32)) Memory (.D(multiplexer_1_out), .C(clk), .Q(sum));  // open: nQ
  D_FF #(.Bits(4)) Memory_2 (.D(multiplexer_2_out), .C(clk), .Q(count));  // open: nQ
  Div #(.Bits(32)) Calculate (.a(sum), .b({{28{1'b0}}, count}), .q({Calculate_q, mean}));  // open: r
endmodule

/* Test case Case1:
clk A input reset mean busy
0 0 0 0 0 0
1 0 0 0 0 0
0 0 0 1 0 0
1 0 0 1 0 0
0 0 0 0 0 0
1 0 0 0 0 0
0 5 1 0 X X
1 5 1 0 X X
0 5 0 0 X X
1 5 0 0 X X
loop(x,500)
end loop
0 0 0 0 5 0
1 0 0 0 5 0
*/

/* Test case Case2:
clk A input reset mean busy
0 0 0 0 0 0
1 0 0 0 0 0
0 0 0 1 0 0
1 0 0 1 0 0
0 0 0 0 0 0
1 0 0 0 0 0
0 5 1 0 X X
1 5 1 0 X X
0 5 0 0 X X
1 5 0 0 X X
loop(x,500)
end loop
0 0 0 0 5 0
1 0 0 0 5 0
0 15 1 0 X X
1 15 1 0 X X
0 15 0 0 X X
1 15 0 0 X X
loop(x,500)
end loop
0 0 0 0 10 0
1 0 0 0 10 0
*/

/* Test case Case3:
clk A input reset mean busy
0 0 0 0 0 0
1 0 0 0 0 0
0 0 0 1 0 0
1 0 0 1 0 0
0 0 0 0 0 0
1 0 0 0 0 0
0 65535 1 0 X X
1 65535 1 0 X X
0 65535 0 0 X X
1 65535 0 0 X X
loop(x,500)
end loop
0 0 0 0 65535 0
1 0 0 0 65535 0
0 65535 1 0 X X
1 65535 1 0 X X
0 65535 0 0 X X
1 65535 0 0 X X
loop(x,500)
end loop
0 0 0 0 65535 0
1 0 0 0 65535 0
*/

/* Test case Case4:
clk A input reset mean busy
0 0 0 0 0 0
1 0 0 0 0 0
0 0 0 1 0 0
1 0 0 1 0 0
0 0 0 0 0 0
1 0 0 0 0 0
0 1 1 0 X X
1 1 1 0 X X
0 1 0 0 X X
1 1 0 0 X X
loop(x,500)
end loop
0 0 0 0 1 0
1 0 0 0 1 0
0 2 1 0 X X
1 2 1 0 X X
0 2 0 0 X X
1 2 0 0 X X
loop(x,500)
end loop
0 0 0 0 1 0
1 0 0 0 1 0
0 3 1 0 X X
1 3 1 0 X X
0 3 0 0 X X
1 3 0 0 X X
loop(x,500)
end loop
0 0 0 0 2 0
1 0 0 0 2 0
0 4 1 0 X X
1 4 1 0 X X
0 4 0 0 X X
1 4 0 0 X X
loop(x,500)
end loop
0 0 0 0 2 0
1 0 0 0 2 0
0 5 1 0 X X
1 5 1 0 X X
0 5 0 0 X X
1 5 0 0 X X
loop(x,500)
end loop
0 0 0 0 3 0
1 0 0 0 3 0
0 6 1 0 X X
1 6 1 0 X X
0 6 0 0 X X
1 6 0 0 X X
loop(x,500)
end loop
0 0 0 0 3 0
1 0 0 0 3 0
0 7 1 0 X X
1 7 1 0 X X
0 7 0 0 X X
1 7 0 0 X X
loop(x,500)
end loop
0 0 0 0 4 0
1 0 0 0 4 0
0 8 1 0 X X
1 8 1 0 X X
0 8 0 0 X X
1 8 0 0 X X
loop(x,500)
end loop
0 0 0 0 4 0
1 0 0 0 4 0
0 9 1 0 X X
1 9 1 0 X X
0 9 0 0 X X
1 9 0 0 X X
loop(x,500)
end loop
0 0 0 0 5 0
1 0 0 0 5 0
0 10 1 0 X X
1 10 1 0 X X
0 10 0 0 X X
1 10 0 0 X X
loop(x,500)
end loop
0 0 0 0 5 0
1 0 0 0 5 0
0 11 1 0 X X
1 11 1 0 X X
0 11 0 0 X X
1 11 0 0 X X
loop(x,500)
end loop
0 0 0 0 6 0
1 0 0 0 6 0
0 12 1 0 X X
1 12 1 0 X X
0 12 0 0 X X
1 12 0 0 X X
loop(x,500)
end loop
0 0 0 0 6 0
1 0 0 0 6 0
0 13 1 0 X X
1 13 1 0 X X
0 13 0 0 X X
1 13 0 0 X X
loop(x,500)
end loop
0 0 0 0 7 0
1 0 0 0 7 0
0 14 1 0 X X
1 14 1 0 X X
0 14 0 0 X X
1 14 0 0 X X
loop(x,500)
end loop
0 0 0 0 7 0
1 0 0 0 7 0
0 15 1 0 X X
1 15 1 0 X X
0 15 0 0 X X
1 15 0 0 X X
loop(x,500)
end loop
0 0 0 0 8 0
1 0 0 0 8 0
*/

/* Test case Case5:
clk A input reset mean busy
0 0 0 0 0 0
1 0 0 0 0 0
0 0 0 1 0 0
1 0 0 1 0 0
0 0 0 0 0 0
1 0 0 0 0 0
0 0 1 0 X X
1 0 1 0 X X
0 0 0 0 X X
1 0 0 0 X X
loop(x,500)
end loop
0 0 0 0 0 0
1 0 0 0 0 0
0 0 1 0 X X
1 0 1 0 X X
0 0 0 0 X X
1 0 0 0 X X
loop(x,500)
end loop
0 0 0 0 0 0
1 0 0 0 0 0
0 0 1 0 X X
1 0 1 0 X X
0 0 0 0 X X
1 0 0 0 X X
loop(x,500)
end loop
0 0 0 0 0 0
1 0 0 0 0 0
0 0 1 0 X X
1 0 1 0 X X
0 0 0 0 X X
1 0 0 0 X X
loop(x,500)
end loop
0 0 0 0 0 0
1 0 0 0 0 0
0 0 1 0 X X
1 0 1 0 X X
0 0 0 0 X X
1 0 0 0 X X
loop(x,500)
end loop
0 0 0 0 0 0
1 0 0 0 0 0
0 0 1 0 X X
1 0 1 0 X X
0 0 0 0 X X
1 0 0 0 X X
loop(x,500)
end loop
0 0 0 0 0 0
1 0 0 0 0 0
0 0 1 0 X X
1 0 1 0 X X
0 0 0 0 X X
1 0 0 0 X X
loop(x,500)
end loop
0 0 0 0 0 0
1 0 0 0 0 0
0 0 1 0 X X
1 0 1 0 X X
0 0 0 0 X X
1 0 0 0 X X
loop(x,500)
end loop
0 0 0 0 0 0
1 0 0 0 0 0
0 0 1 0 X X
1 0 1 0 X X
0 0 0 0 X X
1 0 0 0 X X
loop(x,500)
end loop
0 0 0 0 0 0
1 0 0 0 0 0
0 0 1 0 X X
1 0 1 0 X X
0 0 0 0 X X
1 0 0 0 X X
loop(x,500)
end loop
0 0 0 0 0 0
1 0 0 0 0 0
*/
