// Digital circuit Final_CEDT_2024_01_combinational.dig as structural Verilog
module Final_CEDT_2024_01_combinational (
  input  X,
  input  Y,
  input  Z,
  output A,
  output B,
  output C
);

  wire and_1_out, and_2_out, and_3_out, and_4_out, and_5_out, not_1_out, not_2_out, not_3_out;

  not not_1 (not_1_out, X);
  not not_2 (not_2_out, Y);
  not not_3 (not_3_out, Z);
  and and_1 (and_1_out, not_1_out, Z);
  and and_2 (and_2_out, X, Y, not_3_out);
  and and_3 (and_3_out, not_2_out, Z);
  and and_4 (and_4_out, X, not_2_out);
  and and_5 (and_5_out, X, Z);
  or or_1 (A, and_1_out, and_2_out, and_3_out);
  or or_2 (B, and_4_out, not_3_out);
  or or_3 (C, and_5_out, Y);
endmodule
