// Digital circuit Final_CEDT_2024_01_flipflop.dig as structural Verilog
module Final_CEDT_2024_01_flipflop (
  input  X,
  input  Y,
  input  Z,
  input  clock,
  output A,
  output B,
  output C
);

  wire and_1_out, and_2_out, and_3_out, and_4_out, and_5_out, not_1_out, not_2_out, not_3_out, or_1_out,
       or_2_out, or_3_out;

  not not_1 (not_1_out, A);
  not not_2 (not_2_out, B);
  not not_3 (not_3_out, C);
  and and_1 (and_1_out, not_1_out, C);
  and and_2 (and_2_out, A, B, not_3_out);
  and and_3 (and_3_out, not_2_out, C);
  and and_4 (and_4_out, A, not_2_out);
  and and_5 (and_5_out, A, C);
  or or_1 (or_1_out, and_1_out, and_2_out, and_3_out);
  or or_2 (or_2_out, and_4_out, not_3_out);
  or or_3 (or_3_out, and_5_out, B);
  D_FF d_ff_1 (.D(or_1_out), .C(clock), .Q(A));  // open: nQ
  D_FF d_ff_2 (.D(or_2_out), .C(clock), .Q(B));  // open: nQ
  D_FF d_ff_3 (.D(or_3_out), .C(clock), .Q(C));  // open: nQ
endmodule
