// Digital circuit Final_CEDT_2024_02_calculate.dig as structural Verilog
module Final_CEDT_2024_02_calculate (
  output [15:0] H,
  output [15:0] W,
  output [15:0] H_2,
  output [15:0] W_2
);

  wire [15:0] div_1_r, div_2_q, div_3_r, div_4_q;

  Div #(.Bits(16)) div_1 (.a(16'h40), .b(16'h4), .q(H), .r(div_1_r));
  Div #(.Bits(16)) div_2 (.a(div_1_r), .b(16'h2), .q(div_2_q));  // open: r
  Add #(.Bits(16)) add_1 (.a(H), .b(div_2_q), .c_i(1'b0), .s(W));  // open: c_o
  Div #(.Bits(16)) div_3 (.a(16'h42), .b(16'h4), .q(H_2), .r(div_3_r));
  Div #(.Bits(16)) div_4 (.a(div_3_r), .b(16'h2), .q(div_4_q));  // open: r
  Add #(.Bits(16)) add_2 (.a(H_2), .b(div_4_q), .c_i(1'b0), .s(W_2));  // open: c_o

  // Notes on the sheet:
  //   64 = 2(16 + 16)
  //   66 = 2(17 + 16)
endmodule
