// Digital circuit Final_CEDT_2024_02_calculate2.dig as structural Verilog
module Final_CEDT_2024_02_calculate2 (
  input  [15:0] P,
  output [15:0] H,
  output [15:0] W,
  output [31:0] A
);

  wire [15:0] div_1_q, Height_r;

  Div #(.Bits(16)) Height (.a(P), .b(16'h4), .q(H), .r(Height_r));
  Div #(.Bits(16)) div_1 (.a(Height_r), .b(16'h2), .q(div_1_q));  // open: r
  Add #(.Bits(16)) Width (.a(H), .b(div_1_q), .c_i(1'b0), .s(W));  // open: c_o
  Mul #(.Bits(16)) Area (.a(H), .b(W), .mul(A));
endmodule
