// Digital circuit Final_CEDT_2024_02_flipflop.dig as structural Verilog
module Final_CEDT_2024_02_flipflop (
  input  [15:0] P,
  input  clock,
  output [15:0] H,
  output [15:0] W,
  output [31:0] A
);

  wire [15:0] div_1_q, Height_q, Height_r, Width_s;
  wire [31:0] Area_mul;

  Div #(.Bits(16)) Height (.a(P), .b(16'h4), .q(Height_q), .r(Height_r));
  Div #(.Bits(16)) div_1 (.a(Height_r), .b(16'h2), .q(div_1_q));  // open: r
  Add #(.Bits(16)) Width (.a(Height_q), .b(div_1_q), .c_i(1'b0), .s(Width_s));  // open: c_o
  Mul #(.Bits(16)) Area (.a(Height_q), .b(Width_s), .mul(Area_mul));
  D_FF #(.Bits(16)) d_ff_1 (.D(Height_q), .C(clock), .Q(H));  // open: nQ
  D_FF #(.Bits(16)) d_ff_2 (.D(Width_s), .C(clock), .Q(W));  // open: nQ
  D_FF #(.Bits(32)) d_ff_3 (.D(Area_mul), .C(clock), .Q(A));  // open: nQ
endmodule
