// Digital circuit Final_CEDT_2024_02_start2.dig as structural Verilog
module Final_CEDT_2024_02_start2 (
  input  start,
  input  [15:0] P,
  input  clock,
  output [15:0] H,
  output [15:0] W,
  output [31:0] A,
  output busy
);

  wire d_ff_1_nq, d_ff_2_q, d_ff_3_q;
  wire [15:0] d_ff_4_q, d_ff_5_q, div_1_q, Height_q, Height_r, Width_s;
  wire [31:0] Area_mul, d_ff_6_q;

  Div #(.Bits(16)) Height (.a(P), .b(16'h4), .q(Height_q), .r(Height_r));
  D_FF d_ff_1 (.D(start), .C(clock), .nQ(d_ff_1_nq));  // open: Q
  Div #(.Bits(16)) div_1 (.a(Height_r), .b(16'h2), .q(div_1_q));  // open: r
  D_FF d_ff_2 (.D(start), .C(clock), .Q(d_ff_2_q));  // open: nQ
  D_FF d_ff_3 (.D(d_ff_1_nq), .C(clock), .Q(d_ff_3_q));  // open: nQ
  Add #(.Bits(16)) Width (.a(Height_q), .b(div_1_q), .c_i(1'b0), .s(Width_s));  // open: c_o
  and and_1 (busy, d_ff_2_q, d_ff_3_q);
  Mul #(.Bits(16)) Area (.a(Height_q), .b(Width_s), .mul(Area_mul));
  D_FF #(.Bits(16)) d_ff_4 (.D(Height_q), .C(busy), .Q(d_ff_4_q));  // open: nQ
  D_FF #(.Bits(16)) d_ff_5 (.D(Width_s), .C(busy), .Q(d_ff_5_q));  // open: nQ
  D_FF #(.Bits(32)) d_ff_6 (.D(Area_mul), .C(busy), .Q(d_ff_6_q));  // open: nQ
  D_FF #(.Bits(16)) d_ff_7 (.D(d_ff_4_q), .C(clock), .Q(H));  // open: nQ
  D_FF #(.Bits(16)) d_ff_8 (.D(d_ff_5_q), .C(clock), .Q(W));  // open: nQ
  D_FF #(.Bits(32)) d_ff_9 (.D(d_ff_6_q), .C(clock), .Q(A));  // open: nQ
endmodule
