// Digital circuit Final_CEDT_2024_03.dig as structural Verilog
module Final_CEDT_2024_03 (
  input  [7:0] N,
  input  clock,
  input  \new ,
  input  reset,
  output [7:0] max,
  output busy,
  output [7:0] num_inc
);

  wire and_1_out, Compare_gt, d_ff_1_nq, d_ff_2_q, d_ff_3_q, not_1_out;
  wire [7:0] Add_1_s, Enable_2_q, Enable_q, Load_q, multiplexer_1_out, multiplexer_2_out;

  not not_1 (not_1_out, reset);
  D_FF #(.Bits(8)) Load (.D(N), .C(busy), .Q(Load_q));  // open: nQ
  and and_1 (and_1_out, not_1_out, \new );
  Comparator #(.Bits(8)) Compare (.a(Load_q), .b(max), .gt(Compare_gt));  // open: eq, lt
  Add #(.Bits(8)) Add_1 (.a(num_inc), .b(8'h1), .c_i(1'b0), .s(Add_1_s));  // open: c_o
  D_FF d_ff_1 (.D(and_1_out), .C(clock), .nQ(d_ff_1_nq));  // open: Q
  D_FF #(.Bits(8)) Enable (.D(Load_q), .C(Compare_gt), .Q(Enable_q));  // open: nQ
  D_FF #(.Bits(8)) Enable_2 (.D(Add_1_s), .C(Compare_gt), .Q(Enable_2_q));  // open: nQ
  D_FF d_ff_2 (.D(and_1_out), .C(clock), .Q(d_ff_2_q));  // open: nQ
  D_FF d_ff_3 (.D(d_ff_1_nq), .C(clock), .Q(d_ff_3_q));  // open: nQ
  and and_2 (busy, d_ff_2_q, d_ff_3_q);
  Multiplexer #(.Bits(8)) multiplexer_1 (.sel(reset), .in_0(Enable_q), .in_1({8{1'b0}}), .out(multiplexer_1_out));
  Multiplexer #(.Bits(8)) multiplexer_2 (.sel(reset), .in_0(Enable_2_q), .in_1({8{1'b0}}), .out(multiplexer_2_out));
  D_FF #(.Bits(8)) Memory (.D(multiplexer_1_out), .C(clock), .Q(max));  // open: nQ
  D_FF #(.Bits(8)) Memory_2 (.D(multiplexer_2_out), .C(clock), .Q(num_inc));  // open: nQ
endmodule

/* Test case CEDT03:
N new reset clock num_inc max busy
0 0 1 0 x x x
0 0 1 1 0 0 0
131 1 0 0 x x x
131 1 0 1 x x x
0 0 0 0 x x x
0 0 0 1 x x x
0 0 0 0 x x x
0 0 0 1 x x x
0 0 0 0 x x x
0 0 0 1 x x x
0 0 0 0 x x x
0 0 0 1 x x x
0 0 0 0 x x x
0 0 0 1 x x x
0 0 0 0 x x x
0 0 0 1 x x x
0 0 0 0 x x x
0 0 0 1 x x x
0 0 0 0 x x x
0 0 0 1 x x x
0 0 0 0 x x x
0 0 0 1 x x x
0 0 0 0 x x x
0 0 0 1 x x x
0 0 0 0 x x x
0 0 0 1 x x x
0 0 0 0 x x x
0 0 0 1 x x x
0 0 0 0 x x x
0 0 0 1 x x x
0 0 0 0 x x x
0 0 0 1 x x x
0 0 0 0 x x x
0 0 0 1 x x x
0 0 0 0 x x x
0 0 0 1 x x x
0 0 0 0 x x x
0 0 0 1 x x x
0 0 0 0 x x x
0 0 0 1 x x x
0 0 0 0 x x x
0 0 0 1 x x x
0 0 0 0 x x x
0 0 0 1 x x x
0 0 0 0 x x x
0 0 0 1 x x x
0 0 0 0 x x x
0 0 0 1 x x x
0 0 0 0 x x x
0 0 0 1 x x x
0 0 0 0 x x x
0 0 0 1 x x x
0 0 0 0 x x x
0 0 0 1 x x x
0 0 0 0 x x x
0 0 0 1 x x x
0 0 0 0 x x x
0 0 0 1 x x x
0 0 0 0 x x x
0 0 0 1 x x x
0 0 0 0 x x x
0 0 0 1 x x x
0 0 0 0 x x x
0 0 0 1 x x x
0 0 0 0 1 131 0
0 0 0 1 1 131 0
130 1 0 0 x x x
130 1 0 1 x x x
0 0 0 0 x x x
0 0 0 1 x x x
0 0 0 0 x x x
0 0 0 1 x x x
0 0 0 0 x x x
0 0 0 1 x x x
0 0 0 0 x x x
0 0 0 1 x x x
0 0 0 0 x x x
0 0 0 1 x x x
0 0 0 0 x x x
0 0 0 1 x x x
0 0 0 0 x x x
0 0 0 1 x x x
0 0 0 0 x x x
0 0 0 1 x x x
0 0 0 0 x x x
0 0 0 1 x x x
0 0 0 0 x x x
0 0 0 1 x x x
0 0 0 0 x x x
0 0 0 1 x x x
0 0 0 0 x x x
0 0 0 1 x x x
0 0 0 0 x x x
0 0 0 1 x x x
0 0 0 0 x x x
0 0 0 1 x x x
0 0 0 0 x x x
0 0 0 1 x x x
0 0 0 0 x x x
0 0 0 1 x x x
0 0 0 0 x x x
0 0 0 1 x x x
0 0 0 0 x x x
0 0 0 1 x x x
0 0 0 0 x x x
0 0 0 1 x x x
0 0 0 0 x x x
0 0 0 1 x x x
0 0 0 0 x x x
0 0 0 1 x x x
0 0 0 0 x x x
0 0 0 1 x x x
0 0 0 0 x x x
0 0 0 1 x x x
0 0 0 0 x x x
0 0 0 1 x x x
0 0 0 0 x x x
0 0 0 1 x x x
0 0 0 0 x x x
0 0 0 1 x x x
0 0 0 0 x x x
0 0 0 1 x x x
0 0 0 0 x x x
0 0 0 1 x x x
0 0 0 0 x x x
0 0 0 1 x x x
0 0 0 0 x x x
0 0 0 1 x x x
0 0 0 0 1 131 0
0 0 0 1 1 131 0
58 1 0 0 x x x
58 1 0 1 x x x
0 0 0 0 x x x
0 0 0 1 x x x
0 0 0 0 x x x
0 0 0 1 x x x
0 0 0 0 x x x
0 0 0 1 x x x
0 0 0 0 x x x
0 0 0 1 x x x
0 0 0 0 x x x
0 0 0 1 x x x
0 0 0 0 x x x
0 0 0 1 x x x
0 0 0 0 x x x
0 0 0 1 x x x
0 0 0 0 x x x
0 0 0 1 x x x
0 0 0 0 x x x
0 0 0 1 x x x
0 0 0 0 x x x
0 0 0 1 x x x
0 0 0 0 x x x
0 0 0 1 x x x
0 0 0 0 x x x
0 0 0 1 x x x
0 0 0 0 x x x
0 0 0 1 x x x
0 0 0 0 x x x
0 0 0 1 x x x
0 0 0 0 x x x
0 0 0 1 x x x
0 0 0 0 x x x
0 0 0 1 x x x
0 0 0 0 x x x
0 0 0 1 x x x
0 0 0 0 x x x
0 0 0 1 x x x
0 0 0 0 x x x
0 0 0 1 x x x
0 0 0 0 x x x
0 0 0 1 x x x
0 0 0 0 x x x
0 0 0 1 x x x
0 0 0 0 x x x
0 0 0 1 x x x
0 0 0 0 x x x
0 0 0 1 x x x
0 0 0 0 x x x
0 0 0 1 x x x
0 0 0 0 x x x
0 0 0 1 x x x
0 0 0 0 x x x
0 0 0 1 x x x
0 0 0 0 x x x
0 0 0 1 x x x
0 0 0 0 x x x
0 0 0 1 x x x
0 0 0 0 x x x
0 0 0 1 x x x
0 0 0 0 x x x
0 0 0 1 x x x
0 0 0 0 1 131 0
0 0 0 1 1 131 0
154 1 0 0 x x x
154 1 0 1 x x x
0 0 0 0 x x x
0 0 0 1 x x x
0 0 0 0 x x x
0 0 0 1 x x x
0 0 0 0 x x x
0 0 0 1 x x x
0 0 0 0 x x x
0 0 0 1 x x x
0 0 0 0 x x x
0 0 0 1 x x x
0 0 0 0 x x x
0 0 0 1 x x x
0 0 0 0 x x x
0 0 0 1 x x x
0 0 0 0 x x x
0 0 0 1 x x x
0 0 0 0 x x x
0 0 0 1 x x x
0 0 0 0 x x x
0 0 0 1 x x x
0 0 0 0 x x x
0 0 0 1 x x x
0 0 0 0 x x x
0 0 0 1 x x x
0 0 0 0 x x x
0 0 0 1 x x x
0 0 0 0 x x x
0 0 0 1 x x x
0 0 0 0 x x x
0 0 0 1 x x x
0 0 0 0 x x x
0 0 0 1 x x x
0 0 0 0 x x x
0 0 0 1 x x x
0 0 0 0 x x x
0 0 0 1 x x x
0 0 0 0 x x x
0 0 0 1 x x x
0 0 0 0 x x x
0 0 0 1 x x x
0 0 0 0 x x x
0 0 0 1 x x x
0 0 0 0 x x x
0 0 0 1 x x x
0 0 0 0 x x x
0 0 0 1 x x x
0 0 0 0 x x x
0 0 0 1 x x x
0 0 0 0 x x x
0 0 0 1 x x x
0 0 0 0 x x x
0 0 0 1 x x x
0 0 0 0 x x x
0 0 0 1 x x x
0 0 0 0 x x x
0 0 0 1 x x x
0 0 0 0 x x x
0 0 0 1 x x x
0 0 0 0 x x x
0 0 0 1 x x x
0 0 0 0 2 154 0
0 0 0 1 2 154 0
122 1 0 0 x x x
122 1 0 1 x x x
0 0 0 0 x x x
0 0 0 1 x x x
0 0 0 0 x x x
0 0 0 1 x x x
0 0 0 0 x x x
0 0 0 1 x x x
0 0 0 0 x x x
0 0 0 1 x x x
0 0 0 0 x x x
0 0 0 1 x x x
0 0 0 0 x x x
0 0 0 1 x x x
0 0 0 0 x x x
0 0 0 1 x x x
0 0 0 0 x x x
0 0 0 1 x x x
0 0 0 0 x x x
0 0 0 1 x x x
0 0 0 0 x x x
0 0 0 1 x x x
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*/
