// Digital circuit Final_CEDT_2024_03_compare.dig as structural Verilog
module Final_CEDT_2024_03_compare (
  input  [7:0] N,
  input  clock,
  input  \new ,
  output [7:0] max,
  output busy
);

  wire Compare_gt, d_ff_1_nq, d_ff_2_q, d_ff_3_q;
  wire [7:0] Enable_q, Load_q;

  D_FF d_ff_1 (.D(\new ), .C(clock), .nQ(d_ff_1_nq));  // open: Q
  D_FF #(.Bits(8)) Load (.D(N), .C(busy), .Q(Load_q));  // open: nQ
  Comparator #(.Bits(8)) Compare (.a(Load_q), .b(max), .gt(Compare_gt));  // open: eq, lt
  D_FF d_ff_2 (.D(\new ), .C(clock), .Q(d_ff_2_q));  // open: nQ
  D_FF d_ff_3 (.D(d_ff_1_nq), .C(clock), .Q(d_ff_3_q));  // open: nQ
  and and_1 (busy, d_ff_2_q, d_ff_3_q);
  D_FF #(.Bits(8)) Enable (.D(Load_q), .C(Compare_gt), .Q(Enable_q));  // open: nQ
  D_FF #(.Bits(8)) Memory (.D(Enable_q), .C(clock), .Q(max));  // open: nQ
endmodule
