// Digital circuit Final_CEDT_2024_03_flipflop.dig as structural Verilog
module Final_CEDT_2024_03_flipflop (
  input  [7:0] N,
  input  clock,
  output [7:0] max
);

  D_FF #(.Bits(8)) Memory (.D(N), .C(clock), .Q(max));  // open: nQ
endmodule
