// Digital circuit Final_CEDT_2024_03_new.dig as structural Verilog
module Final_CEDT_2024_03_new (
  input  [7:0] N,
  input  clock,
  input  \new ,
  output [7:0] max,
  output busy
);

  wire d_ff_1_nq, d_ff_2_q, d_ff_3_q;

  D_FF #(.Bits(8)) Memory (.D(N), .C(clock), .Q(max));  // open: nQ
  D_FF d_ff_1 (.D(\new ), .C(clock), .nQ(d_ff_1_nq));  // open: Q
  D_FF d_ff_2 (.D(\new ), .C(clock), .Q(d_ff_2_q));  // open: nQ
  D_FF d_ff_3 (.D(d_ff_1_nq), .C(clock), .Q(d_ff_3_q));  // open: nQ
  and and_1 (busy, d_ff_2_q, d_ff_3_q);
endmodule
