// Digital circuit Final_CP_2023_03.dig as structural Verilog
module Final_CP_2023_03 (
  input  [15:0] A,
  input  \input ,
  input  reset,
  input  clk,
  output [15:0] first,
  output [15:0] second,
  output s1,
  output s2
);

  wire Comp2_gt, not_1_out;
  wire [15:0] Load_2_q, Load_q, multiplexer_1_out, multiplexer_2_out, multiplexer_3_out, multiplexer_4_out,
       multiplexer_5_out;

  Comparator #(.Bits(16)) Comp1 (.a(A), .b(first), .gt(s1));  // open: eq, lt
  Comparator #(.Bits(16)) Comp2 (.a(A), .b(second), .gt(Comp2_gt));  // open: eq, lt
  Multiplexer #(.Bits(16)) multiplexer_1 (.sel(s1), .in_0(first), .in_1(A), .out(multiplexer_1_out));
  Multiplexer #(.Bits(16)) multiplexer_2 (.sel(s1), .in_0(second), .in_1(first), .out(multiplexer_2_out));
  not not_1 (not_1_out, s1);
  Multiplexer #(.Bits(16)) multiplexer_3 (.sel(s2), .in_0(multiplexer_2_out), .in_1(A), .out(multiplexer_3_out));
  and and_1 (s2, not_1_out, Comp2_gt);
  D_FF #(.Bits(16)) Load (.D(multiplexer_1_out), .C(\input ), .Q(Load_q));  // open: nQ
  D_FF #(.Bits(16)) Load_2 (.D(multiplexer_3_out), .C(\input ), .Q(Load_2_q));  // open: nQ
  Multiplexer #(.Bits(16)) multiplexer_4 (.sel(reset), .in_0(Load_q), .in_1({16{1'b0}}), .out(multiplexer_4_out));
  Multiplexer #(.Bits(16)) multiplexer_5 (.sel(reset), .in_0(Load_2_q), .in_1({16{1'b0}}), .out(multiplexer_5_out));
  D_FF #(.Bits(16)) Memory (.D(multiplexer_4_out), .C(clk), .Q(first));  // open: nQ
  D_FF #(.Bits(16)) Memory_2 (.D(multiplexer_5_out), .C(clk), .Q(second));  // open: nQ
endmodule
