// Digital circuit Final_CP_2024_02.dig as structural Verilog
module Final_CP_2024_02 (
  input  [15:0] A,
  input  \input ,
  input  clk,
  input  [3:0] R,
  output busy,
  output [31:0] Product,
  output [15:0] X,
  output [15:0] nroot
);

  wire Compare_eq, Compare_gt, isRoot1, or_1_out, or_2_out;
  wire [15:0] Add_1_s, Minus_1_s, multiplexer_1_out, multiplexer_3_out;
  wire [31:0] multiplexer_5_out, multiplexer_6_out, multiplexer_7_out;
  wire [63:0] R0_mul, R1_mul, R2_mul, R3_mul, X_2_mul, X_4_mul, X_8_mul;

  Add #(.Bits(16)) Add_1 (.a(X), .b(16'h1), .c_i(1'b0), .s(Add_1_s));  // open: c_o
  Sub #(.Bits(16)) Minus_1 (.a(X), .b(16'h1), .c_i(1'b0), .s(Minus_1_s));  // open: c_o
  Comparator #(.Bits(32), .Signed("true")) Compare (
    .a({{16{1'b0}}, A}), .b(Product), .gt(Compare_gt), .eq(Compare_eq));  // open: lt
  Multiplexer #(.Bits(16)) multiplexer_1 (.sel(busy), .in_0(X), .in_1(Add_1_s), .out(multiplexer_1_out));
  Multiplexer #(.Bits(16)) multiplexer_2 (.sel(isRoot1), .in_0(Minus_1_s), .in_1(A), .out(nroot));
  or or_1 (or_1_out, Compare_gt, Compare_eq);
  Comparator #(.Signed("true"), .Bits(4)) Root_1 (.a(R), .b(4'b0001), .eq(isRoot1));  // open: gt, lt
  Multiplexer #(.Bits(16)) multiplexer_3 (
    .sel(\input ), .in_0(multiplexer_1_out), .in_1(16'h2), .out(multiplexer_3_out));
  or or_2 (or_2_out, busy, \input );
  Multiplexer multiplexer_4 (.sel(isRoot1), .in_0(or_1_out), .in_1(1'b0), .out(busy));
  Register #(.Bits(16)) Memory (.D(multiplexer_3_out), .C(clk), .en(or_2_out), .Q(X));
  Mul #(.Bits(32)) X_2 (.a({{16{1'b0}}, X}), .b({{16{1'b0}}, X}), .mul(X_2_mul));
  Mul #(.Bits(32)) X_4 (.a(X_2_mul[31:0]), .b(X_2_mul[31:0]), .mul(X_4_mul));
  Mul #(.Bits(32)) X_8 (.a(X_4_mul[31:0]), .b(X_4_mul[31:0]), .mul(X_8_mul));
  Mul #(.Bits(32)) R0 (.a(32'h1), .b({{16{1'b0}}, X}), .mul(R0_mul));
  Mul #(.Bits(32)) R1 (.a(multiplexer_5_out), .b(X_2_mul[31:0]), .mul(R1_mul));
  Mul #(.Bits(32)) R2 (.a(multiplexer_6_out), .b(X_4_mul[31:0]), .mul(R2_mul));
  Mul #(.Bits(32)) R3 (.a(multiplexer_7_out), .b(X_8_mul[31:0]), .mul(R3_mul));
  Multiplexer #(.Bits(32)) multiplexer_5 (.sel(R[0]), .in_0(32'h1), .in_1(R0_mul[31:0]), .out(multiplexer_5_out));
  Multiplexer #(.Bits(32)) multiplexer_6 (
    .sel(R[1]), .in_0(multiplexer_5_out), .in_1(R1_mul[31:0]), .out(multiplexer_6_out));
  Multiplexer #(.Bits(32)) multiplexer_7 (
    .sel(R[2]), .in_0(multiplexer_6_out), .in_1(R2_mul[31:0]), .out(multiplexer_7_out));
  Multiplexer #(.Bits(32)) multiplexer_8 (.sel(R[3]), .in_0(multiplexer_7_out), .in_1(R3_mul[31:0]), .out(Product));
endmodule

/* Test case TestCase1:
clk A R input nroot busy
0 0 0 0 X 0
1 0 0 0 X 0
0 0 0 0 X 0
1 0 0 0 X 0
0 2 2 1 X X
1 2 2 1 X X
repeat (255) C 2 2 0 X X
0 2 2 0 1 0
1 2 2 0 1 0
0 0 0 0 X 0
1 0 0 0 X 0
0 0 0 0 X 0
1 0 0 0 X 0
0 4 2 1 X X
1 4 2 1 X X
repeat (255) C 4 2 0 X X
0 4 2 0 2 0
1 4 2 0 2 0
0 0 0 0 X 0
1 0 0 0 X 0
0 0 0 0 X 0
1 0 0 0 X 0
0 8 2 1 X X
1 8 2 1 X X
repeat (255) C 8 2 0 X X
0 8 2 0 2 0
1 8 2 0 2 0
0 0 0 0 X 0
1 0 0 0 X 0
0 0 0 0 X 0
1 0 0 0 X 0
0 16 2 1 X X
1 16 2 1 X X
repeat (255) C 16 2 0 X X
0 16 2 0 4 0
1 16 2 0 4 0
*/

/* Test case TestCase4:
clk A R input nroot busy
0 0 0 0 X 0
1 0 0 0 X 0
0 0 0 0 X 0
1 0 0 0 X 0
0 65530 12 1 X X
1 65530 12 1 X X
repeat (255) C 65530 12 0 X X
0 65530 12 0 2 0
1 65530 12 0 2 0
0 0 0 0 X 0
1 0 0 0 X 0
0 0 0 0 X 0
1 0 0 0 X 0
0 60000 3 1 X X
1 60000 3 1 X X
repeat (255) C 60000 3 0 X X
0 60000 3 0 39 0
1 60000 3 0 39 0
0 0 0 0 X 0
1 0 0 0 X 0
0 0 0 0 X 0
1 0 0 0 X 0
0 55124 4 1 X X
1 55124 4 1 X X
repeat (255) C 55124 4 0 X X
0 55124 4 0 15 0
1 55124 4 0 15 0
0 0 0 0 X 0
1 0 0 0 X 0
0 0 0 0 X 0
1 0 0 0 X 0
0 14778 5 1 X X
1 14778 5 1 X X
repeat (255) C 14778 5 0 X X
0 14778 5 0 6 0
1 14778 5 0 6 0
*/

/* Test case TestCase8:
clk A R input nroot busy
0 0 0 0 X 0
1 0 0 0 X 0
0 0 0 0 X 0
1 0 0 0 X 0
0 65535 1 1 X X
1 65535 1 1 X X
repeat (255) C 65535 1 0 X X
0 65535 1 0 65535 0
1 65535 1 0 65535 0
0 0 0 0 X 0
1 0 0 0 X 0
0 0 0 0 X 0
1 0 0 0 X 0
0 64000 15 1 X X
1 64000 15 1 X X
repeat (255) C 64000 15 0 X X
0 64000 15 0 2 0
1 64000 15 0 2 0
0 0 0 0 X 0
1 0 0 0 X 0
0 0 0 0 X 0
1 0 0 0 X 0
0 12000 5 1 X X
1 12000 5 1 X X
repeat (255) C 12000 5 0 X X
0 12000 5 0 6 0
1 12000 5 0 6 0
0 0 0 0 X 0
1 0 0 0 X 0
0 0 0 0 X 0
1 0 0 0 X 0
0 65535 15 1 X X
1 65535 15 1 X X
repeat (255) C 65535 15 0 X X
0 65535 15 0 2 0
1 65535 15 0 2 0
*/
