// Digital circuit sol2.dig as structural Verilog
module sol2 (
  input  [15:0] A,
  input  \input ,
  input  clk,
  input  [3:0] R,
  output busy,
  output [15:0] nroot,
  output [1:0] dat
);

  wire and_1_out, comparator_2_gt, comparator_3_gt, comparator_4_gt, comparator_5_gt, eq0, eq1, eq2, eq3, g0,
       g1, g2, g3, lt0, lt1, lt2, lt3, multiplexer_1_out, not_1_out, or_1_out, or_2_out, or_3_out, or_4_out,
       or_5_out, or_6_out, previnput, REQ1;
  wire [8:0] add_1_s, lm0, lm1, lm2, lm3, multiplexer_2_out, multiplexer_3_out;
  wire [15:0] multiplexer_4_out;
  wire [31:0] multiplexer_5_out, multiplexer_6_out, multiplexer_7_out, multiplexer_8_out, multiplexer_9_out,
       multiplexer_10_out, multiplexer_11_out, multiplexer_12_out, multiplexer_13_out, multiplexer_14_out,
       multiplexer_15_out, multiplexer_16_out, multiplexer_17_out, multiplexer_18_out, multiplexer_19_out,
       multiplexer_20_out, PT1, PT2, PT3, PT4, T1, T2, T3;
  wire [63:0] mul_4_mul, mul_5_mul, mul_6_mul, mul_7_mul, mul_8_mul, mul_9_mul, mul_11_mul, mul_13_mul,
       mul_14_mul, mul_15_mul, mul_16_mul, mul_17_mul, mul_18_mul, mul_19_mul, mul_20_mul, mul_21_mul,
       mul_23_mul;
  wire [63:32] mul_1_mul, mul_2_mul, mul_3_mul, mul_10_mul, mul_12_mul, mul_22_mul, mul_24_mul;

  Register register_1 (.D(\input ), .C(clk), .en(1'b1), .Q(previnput));
  or or_1 (or_1_out, eq0, lt0, eq1, lt1, REQ1, eq2, lt2, eq3, lt3);
  and and_1 (and_1_out, \input , ~previnput);  // And
  not not_1 (not_1_out, or_1_out);
  Multiplexer multiplexer_1 (.sel(busy), .in_0(and_1_out), .in_1(not_1_out), .out(multiplexer_1_out));
  Multiplexer #(.Bits(9)) multiplexer_2 (.sel(busy), .in_0({9{1'b0}}), .in_1(add_1_s), .out(multiplexer_2_out));
  Register #(.Bits(9)) register_2 (.D(multiplexer_2_out), .C(clk), .en(1'b1), .Q(lm0));
  Add #(.Bits(9)) add_1 (.a(lm0), .b(9'h4), .c_i(1'b0), .s(add_1_s));  // open: c_o
  Add #(.Bits(9)) add_2 (.a(lm0), .b(9'h1), .c_i(1'b0), .s(lm1));  // open: c_o
  Add #(.Bits(9)) add_3 (.a(lm0), .b(9'h2), .c_i(1'b0), .s(lm2));  // open: c_o
  Add #(.Bits(9)) add_4 (.a(lm0), .b(9'h3), .c_i(1'b0), .s(lm3));  // open: c_o
  Register register_3 (.D(multiplexer_1_out), .C(clk), .en(1'b1), .Q(busy));
  Comparator #(.Bits(4)) comparator_1 (.a(R), .b(4'b0001), .eq(REQ1));  // open: gt, lt
  Multiplexer #(.Selector_Bits(2), .Bits(9)) multiplexer_3 (
    .sel(dat), .in_0(lm0), .in_1(lm1), .in_2(lm2), .in_3(lm3), .out(multiplexer_3_out));
  Mul #(.Bits(32)) mul_1 (.a({{23{1'b0}}, lm0}), .b({{23{1'b0}}, lm0}), .mul({mul_1_mul, T1}));
  Mul #(.Bits(32)) mul_2 (.a(T1), .b(T1), .mul({mul_2_mul, T2}));
  Mul #(.Bits(32)) mul_3 (.a(T2), .b(T2), .mul({mul_3_mul, T3}));
  Mul #(.Bits(32)) mul_4 (.a({{23{1'b0}}, lm2}), .b({{23{1'b0}}, lm2}), .mul(mul_4_mul));
  Mul #(.Bits(32)) mul_5 (.a(mul_4_mul[31:0]), .b(mul_4_mul[31:0]), .mul(mul_5_mul));
  Mul #(.Bits(32)) mul_6 (.a(mul_5_mul[31:0]), .b(mul_5_mul[31:0]), .mul(mul_6_mul));
  Comparator #(.Bits(32)) comparator_2 (.a({{16{1'b0}}, A}), .b(PT1), .gt(comparator_2_gt), .eq(eq0), .lt(lt0));
  Comparator #(.Bits(32)) comparator_3 (.a({{16{1'b0}}, A}), .b(PT2), .gt(comparator_3_gt), .eq(eq1), .lt(lt1));
  Comparator #(.Bits(32)) comparator_4 (.a({{16{1'b0}}, A}), .b(PT3), .gt(comparator_4_gt), .eq(eq2), .lt(lt2));
  Comparator #(.Bits(32)) comparator_5 (.a({{16{1'b0}}, A}), .b(PT4), .gt(comparator_5_gt), .eq(eq3), .lt(lt3));
  Multiplexer #(.Bits(16)) multiplexer_4 (
    .sel(REQ1), .in_0({{7{1'b0}}, multiplexer_3_out}), .in_1(A), .out(multiplexer_4_out));
  or or_2 (or_2_out, comparator_2_gt, eq0);
  or or_3 (or_3_out, comparator_3_gt, eq1);
  or or_4 (or_4_out, comparator_4_gt, eq2);
  or or_5 (or_5_out, comparator_5_gt, eq3);
  Register #(.Bits(16)) register_4 (.D(multiplexer_4_out), .C(clk), .en(or_6_out), .Q(nroot));
  Multiplexer #(.Bits(32)) multiplexer_5 (.sel(R[0]), .in_0(32'h1), .in_1({{23{1'b0}}, lm0}), .out(multiplexer_5_out));
  Multiplexer #(.Bits(32)) multiplexer_6 (.sel(R[1]), .in_0(32'h1), .in_1(T1), .out(multiplexer_6_out));
  Multiplexer #(.Bits(32)) multiplexer_7 (.sel(R[2]), .in_0(32'h1), .in_1(T2), .out(multiplexer_7_out));
  Multiplexer #(.Bits(32)) multiplexer_8 (.sel(R[3]), .in_0(32'h1), .in_1(T3), .out(multiplexer_8_out));
  Multiplexer #(.Bits(32)) multiplexer_9 (.sel(R[0]), .in_0(32'h1), .in_1({{23{1'b0}}, lm2}), .out(multiplexer_9_out));
  Multiplexer #(.Bits(32)) multiplexer_10 (.sel(R[1]), .in_0(32'h1), .in_1(mul_4_mul[31:0]), .out(multiplexer_10_out));
  Multiplexer #(.Bits(32)) multiplexer_11 (.sel(R[2]), .in_0(32'h1), .in_1(mul_5_mul[31:0]), .out(multiplexer_11_out));
  Multiplexer #(.Bits(32)) multiplexer_12 (.sel(R[3]), .in_0(32'h1), .in_1(mul_6_mul[31:0]), .out(multiplexer_12_out));
  and and_2 (g0, or_2_out, busy);
  and and_3 (g1, or_3_out, busy);
  and and_4 (g2, or_4_out, busy);
  and and_5 (g3, or_5_out, busy);
  Mul #(.Bits(32)) mul_7 (.a(multiplexer_5_out), .b(multiplexer_6_out), .mul(mul_7_mul));
  Mul #(.Bits(32)) mul_8 (.a(multiplexer_9_out), .b(multiplexer_10_out), .mul(mul_8_mul));
  Mul #(.Bits(32)) mul_9 (.a(mul_7_mul[31:0]), .b(multiplexer_7_out), .mul(mul_9_mul));
  Mul #(.Bits(32)) mul_10 (.a(mul_9_mul[31:0]), .b(multiplexer_8_out), .mul({mul_10_mul, PT1}));
  Mul #(.Bits(32)) mul_11 (.a(mul_8_mul[31:0]), .b(multiplexer_11_out), .mul(mul_11_mul));
  Mul #(.Bits(32)) mul_12 (.a(mul_11_mul[31:0]), .b(multiplexer_12_out), .mul({mul_12_mul, PT3}));
  or or_6 (or_6_out, g0, g1, g2, g3);
  PriorityEncoder #(.Selector_Bits(2)) priorityencoder_1 (
    .in0(g0), .in1(g1), .in2(g2), .in3(g3), .num(dat));  // open: any
  Mul #(.Bits(32)) mul_13 (.a({{23{1'b0}}, lm1}), .b({{23{1'b0}}, lm1}), .mul(mul_13_mul));
  Mul #(.Bits(32)) mul_14 (.a(mul_13_mul[31:0]), .b(mul_13_mul[31:0]), .mul(mul_14_mul));
  Mul #(.Bits(32)) mul_15 (.a(mul_14_mul[31:0]), .b(mul_14_mul[31:0]), .mul(mul_15_mul));
  Mul #(.Bits(32)) mul_16 (.a({{23{1'b0}}, lm3}), .b({{23{1'b0}}, lm3}), .mul(mul_16_mul));
  Mul #(.Bits(32)) mul_17 (.a(mul_16_mul[31:0]), .b(mul_16_mul[31:0]), .mul(mul_17_mul));
  Mul #(.Bits(32)) mul_18 (.a(mul_17_mul[31:0]), .b(mul_17_mul[31:0]), .mul(mul_18_mul));
  Multiplexer #(.Bits(32)) multiplexer_13 (
    .sel(R[0]), .in_0(32'h1), .in_1({{23{1'b0}}, lm1}), .out(multiplexer_13_out));
  Multiplexer #(.Bits(32)) multiplexer_14 (.sel(R[1]), .in_0(32'h1), .in_1(mul_13_mul[31:0]), .out(multiplexer_14_out));
  Multiplexer #(.Bits(32)) multiplexer_15 (.sel(R[2]), .in_0(32'h1), .in_1(mul_14_mul[31:0]), .out(multiplexer_15_out));
  Multiplexer #(.Bits(32)) multiplexer_16 (.sel(R[3]), .in_0(32'h1), .in_1(mul_15_mul[31:0]), .out(multiplexer_16_out));
  Multiplexer #(.Bits(32)) multiplexer_17 (
    .sel(R[0]), .in_0(32'h1), .in_1({{23{1'b0}}, lm3}), .out(multiplexer_17_out));
  Multiplexer #(.Bits(32)) multiplexer_18 (.sel(R[1]), .in_0(32'h1), .in_1(mul_16_mul[31:0]), .out(multiplexer_18_out));
  Multiplexer #(.Bits(32)) multiplexer_19 (.sel(R[2]), .in_0(32'h1), .in_1(mul_17_mul[31:0]), .out(multiplexer_19_out));
  Multiplexer #(.Bits(32)) multiplexer_20 (.sel(R[3]), .in_0(32'h1), .in_1(mul_18_mul[31:0]), .out(multiplexer_20_out));
  Mul #(.Bits(32)) mul_19 (.a(multiplexer_13_out), .b(multiplexer_14_out), .mul(mul_19_mul));
  Mul #(.Bits(32)) mul_20 (.a(multiplexer_17_out), .b(multiplexer_18_out), .mul(mul_20_mul));
  Mul #(.Bits(32)) mul_21 (.a(mul_19_mul[31:0]), .b(multiplexer_15_out), .mul(mul_21_mul));
  Mul #(.Bits(32)) mul_22 (.a(mul_21_mul[31:0]), .b(multiplexer_16_out), .mul({mul_22_mul, PT2}));
  Mul #(.Bits(32)) mul_23 (.a(mul_20_mul[31:0]), .b(multiplexer_19_out), .mul(mul_23_mul));
  Mul #(.Bits(32)) mul_24 (.a(mul_23_mul[31:0]), .b(multiplexer_20_out), .mul({mul_24_mul, PT4}));

  // Other names for the same wires on the sheet: Apad[15:0] = A; state = busy

  // Notes on the sheet:
  //   clk: Hz: 20
endmodule

/* Test case TestCase1:
clk A R input nroot busy
0 0 0 0 0 0
1 0 0 0 0 0
0 0 0 0 0 0
1 0 0 0 0 0
0 10 3 1 X X
1 10 3 1 X X
repeat (255) C 10 3 0 X X
0 10 3 0 2 0
1 10 3 0 2 0
*/

/* Test case TestCase2:
clk A R input nroot busy
0 0 0 0 0 0
1 0 0 0 0 0
0 0 0 0 0 0
1 0 0 0 0 0
0 256 4 1 X X
1 256 4 1 X X
repeat (255) C 256 4 0 X X
0 256 4 0 4 0
1 256 4 0 4 0
*/

/* Test case TestCase3:
clk A R input nroot busy
0 0 0 0 X 0
1 0 0 0 X 0
0 0 0 0 X 0
1 0 0 0 X 0
0 4 2 1 X X
1 4 2 1 X X
repeat (255) C 4 2 0 X X
0 4 2 0 2 0
1 4 2 0 2 0
0 0 0 0 X 0
1 0 0 0 X 0
0 0 0 0 X 0
1 0 0 0 X 0
0 1492 3 1 X X
1 1492 3 1 X X
repeat (255) C 1492 3 0 X X
0 1492 3 0 11 0
1 1492 3 0 11 0
*/
