// Digital circuit sol2_02.dig as structural Verilog
module sol2_02 (
  input  [15:0] A,
  input  \input ,
  input  clk,
  input  [3:0] R,
  output [15:0] nroot,
  output busy
);

  wire and_2_out, and_3_out, busy_t, comparator_1_gt, comparator_4_lt, eq, not_2_out, not_3_out, not_4_out,
       or_1_out, or_2_out, or_4_out, or_5_out, or_6_out, t1, t2, t3, t4, t5, t6;
  wire [15:0] add_1_s, d_ff_1_q, d_ff_2_q, mul_1_mul, mul_4_mul, mul_5_mul, multiplexer_1_out,
       multiplexer_2_out, multiplexer_3_out, multiplexer_5_out, multiplexer_6_out, sub_1_s;
  wire [31:0] mul_2_mul, mul_3_mul, mul_6_mul;
  wire [31:16] mul_1_mul_2, mul_4_mul_2, mul_5_mul_2;

  Comparator #(.Bits(4)) comparator_1 (.a(R), .b(4'b0001), .gt(comparator_1_gt));  // open: eq, lt
  not not_1 (eq, comparator_1_gt);
  Multiplexer #(.Bits(16)) multiplexer_1 (.sel(\input ), .in_0(add_1_s), .in_1(16'h2), .out(multiplexer_1_out));
  Add #(.Bits(16)) add_1 (.a(d_ff_1_q), .b(16'h1), .c_i(1'b0), .s(add_1_s));  // open: c_o
  D_FF #(.Bits(16), .Default(2)) d_ff_1 (.D(multiplexer_1_out), .C(clk), .Q(d_ff_1_q));  // open: nQ
  Sub #(.Bits(16)) sub_1 (.a(d_ff_1_q), .b(16'h1), .c_i(1'b0), .s(sub_1_s));  // open: c_o
  not not_2 (not_2_out, busy_t);
  Mul #(.Bits(16)) mul_1 (.a(multiplexer_2_out), .b(multiplexer_3_out), .mul({mul_1_mul_2, mul_1_mul}));
  Multiplexer #(.Bits(16)) multiplexer_2 (.sel(R[0]), .in_0(16'h1), .in_1(d_ff_1_q), .out(multiplexer_2_out));
  Mul #(.Bits(16)) mul_2 (.a(d_ff_1_q), .b(d_ff_1_q), .mul(mul_2_mul));
  D_FF #(.Bits(16)) d_ff_2 (.D(sub_1_s), .C(not_2_out), .Q(d_ff_2_q));  // open: nQ
  Comparator #(.Bits(16)) comparator_2 (.a(mul_1_mul_2), .b({16{1'b0}}), .eq(t4));  // open: gt, lt
  Multiplexer #(.Bits(16)) multiplexer_3 (.sel(R[1]), .in_0(16'h1), .in_1(mul_2_mul[15:0]), .out(multiplexer_3_out));
  Mul #(.Bits(16)) mul_3 (.a(mul_2_mul[15:0]), .b(mul_2_mul[15:0]), .mul(mul_3_mul));
  Comparator #(.Bits(16)) comparator_3 (.a(mul_2_mul[31:16]), .b({16{1'b0}}), .eq(t1));  // open: gt, lt
  Multiplexer #(.Bits(16)) multiplexer_4 (.sel(eq), .in_0(d_ff_2_q), .in_1(A), .out(nroot));
  Comparator #(.Bits(16)) comparator_4 (.a(A), .b(mul_4_mul), .lt(comparator_4_lt));  // open: gt, eq
  Mul #(.Bits(16)) mul_4 (.a(mul_1_mul), .b(mul_5_mul), .mul({mul_4_mul_2, mul_4_mul}));
  not not_3 (not_3_out, comparator_4_lt);
  not not_4 (not_4_out, eq);
  Comparator #(.Bits(16)) comparator_5 (.a(mul_4_mul_2), .b({16{1'b0}}), .eq(t6));  // open: gt, lt
  Mul #(.Bits(16)) mul_5 (.a(multiplexer_5_out), .b(multiplexer_6_out), .mul({mul_5_mul_2, mul_5_mul}));
  Multiplexer #(.Bits(16)) multiplexer_5 (.sel(R[2]), .in_0(16'h1), .in_1(mul_3_mul[15:0]), .out(multiplexer_5_out));
  Mul #(.Bits(16)) mul_6 (.a(mul_3_mul[15:0]), .b(mul_3_mul[15:0]), .mul(mul_6_mul));
  Comparator #(.Bits(16)) comparator_6 (.a(mul_3_mul[31:16]), .b({16{1'b0}}), .eq(t2));  // open: gt, lt
  and and_1 (busy, not_3_out, and_3_out, not_4_out);
  Comparator #(.Bits(16)) comparator_7 (.a(mul_5_mul_2), .b({16{1'b0}}), .eq(t5));  // open: gt, lt
  Multiplexer #(.Bits(16)) multiplexer_6 (.sel(R[3]), .in_0(16'h1), .in_1(mul_6_mul[15:0]), .out(multiplexer_6_out));
  Comparator #(.Bits(16)) comparator_8 (.a(mul_6_mul[31:16]), .b({16{1'b0}}), .eq(t3));  // open: gt, lt
  and and_2 (and_2_out, clk, busy);
  or or_1 (or_1_out, R[2], R[3]);
  or or_2 (or_2_out, R[1], R[2], R[3]);
  or or_3 (busy_t, \input , and_2_out);
  or or_4 (or_4_out, t3, ~R[3]);  // Or
  or or_5 (or_5_out, t2, ~or_1_out);  // Or
  or or_6 (or_6_out, t1, ~or_2_out);  // Or
  and and_3 (and_3_out, t6, t5, t4, or_4_out, or_5_out, or_6_out);

  // Other names for the same wires on the sheet: _0 = R[0]; _1 = R[1]; _2 = R[2]; _3 = R[3]; reset = \input 

  // Notes on the sheet:
  //   A: default 1000
  //   clk: Hz: 50000
  //   R: default 2
endmodule

/* Test case TestCase1:
clk A R input nroot busy
0 0 0 0 X 0
1 0 0 0 X 0
0 0 0 0 X 0
1 0 0 0 X 0
0 2 2 1 X X
1 2 2 1 X X
repeat (255) C 2 2 0 X X
0 2 2 0 1 0
1 2 2 0 1 0
0 0 0 0 X 0
1 0 0 0 X 0
0 0 0 0 X 0
1 0 0 0 X 0
0 4 2 1 X X
1 4 2 1 X X
repeat (255) C 4 2 0 X X
0 4 2 0 2 0
1 4 2 0 2 0
0 0 0 0 X 0
1 0 0 0 X 0
0 0 0 0 X 0
1 0 0 0 X 0
0 8 2 1 X X
1 8 2 1 X X
repeat (255) C 8 2 0 X X
0 8 2 0 2 0
1 8 2 0 2 0
0 0 0 0 X 0
1 0 0 0 X 0
0 0 0 0 X 0
1 0 0 0 X 0
0 16 2 1 X X
1 16 2 1 X X
repeat (255) C 16 2 0 X X
0 16 2 0 4 0
1 16 2 0 4 0
*/

/* Test case TestCase4:
clk A R input nroot busy
0 0 0 0 X 0
1 0 0 0 X 0
0 0 0 0 X 0
1 0 0 0 X 0
0 65530 12 1 X X
1 65530 12 1 X X
repeat (255) C 65530 12 0 X X
0 65530 12 0 2 0
1 65530 12 0 2 0
0 0 0 0 X 0
1 0 0 0 X 0
0 0 0 0 X 0
1 0 0 0 X 0
0 60000 3 1 X X
1 60000 3 1 X X
repeat (255) C 60000 3 0 X X
0 60000 3 0 39 0
1 60000 3 0 39 0
0 0 0 0 X 0
1 0 0 0 X 0
0 0 0 0 X 0
1 0 0 0 X 0
0 55124 4 1 X X
1 55124 4 1 X X
repeat (255) C 55124 4 0 X X
0 55124 4 0 15 0
1 55124 4 0 15 0
0 0 0 0 X 0
1 0 0 0 X 0
0 0 0 0 X 0
1 0 0 0 X 0
0 14778 5 1 X X
1 14778 5 1 X X
repeat (255) C 14778 5 0 X X
0 14778 5 0 6 0
1 14778 5 0 6 0
*/

/* Test case TestCase8:
clk A R input nroot busy
0 0 0 0 X 0
1 0 0 0 X 0
0 0 0 0 X 0
1 0 0 0 X 0
0 65535 1 1 X X
1 65535 1 1 X X
repeat (255) C 65535 1 0 X X
0 65535 1 0 65535 0
1 65535 1 0 65535 0
0 0 0 0 X 0
1 0 0 0 X 0
0 0 0 0 X 0
1 0 0 0 X 0
0 64000 15 1 X X
1 64000 15 1 X X
repeat (255) C 64000 15 0 X X
0 64000 15 0 2 0
1 64000 15 0 2 0
0 0 0 0 X 0
1 0 0 0 X 0
0 0 0 0 X 0
1 0 0 0 X 0
0 12000 5 1 X X
1 12000 5 1 X X
repeat (255) C 12000 5 0 X X
0 12000 5 0 6 0
1 12000 5 0 6 0
0 0 0 0 X 0
1 0 0 0 X 0
0 0 0 0 X 0
1 0 0 0 X 0
0 65535 15 1 X X
1 65535 15 1 X X
repeat (255) C 65535 15 0 X X
0 65535 15 0 2 0
1 65535 15 0 2 0
*/
