// Digital circuit sol2_03.dig as structural Verilog
module sol2_03 (
  input  [15:0] A,
  input  \input ,
  input  clk,
  input  [3:0] R,
  output [15:0] nroot,
  output busy
);

  wire and_1_out, and_2_out, and_3_out, and_4_out, and_5_out, and_6_out, and_7_out, and_8_out, and_9_out,
       and_10_out, and_11_out, and_12_out, and_13_out, and_14_out, and_15_out, and_16_out, comparator_1_eq,
       comparator_1_gt, comparator_2_gt, comparator_3_eq, comparator_3_lt, comparator_4_gt, comparator_5_eq,
       comparator_5_lt, comparator_6_gt, comparator_7_eq, comparator_7_lt, comparator_8_eq, comparator_9_gt,
       comparator_10_eq, comparator_10_lt, comparator_11_gt, comparator_12_eq, comparator_12_lt,
       comparator_13_gt, comparator_14_eq, comparator_14_lt, comparator_15_gt, comparator_16_eq,
       comparator_16_lt, comparator_17_gt, comparator_18_eq, comparator_18_lt, comparator_19_gt,
       comparator_20_eq, comparator_20_lt, comparator_21_gt, comparator_22_eq, comparator_22_lt,
       comparator_23_gt, comparator_24_eq, comparator_24_lt, comparator_25_gt, comparator_26_eq,
       comparator_26_lt, comparator_27_gt, comparator_28_eq, comparator_28_lt, comparator_29_gt,
       comparator_30_eq, comparator_30_lt, comparator_31_gt, comparator_32_eq, comparator_32_lt,
       comparator_33_gt, comparator_34_eq, comparator_34_lt, or_1_out, or_2_out, or_3_out, or_4_out,
       or_5_out, or_6_out, or_7_out, or_8_out, or_9_out, or_10_out, or_11_out, or_12_out, or_13_out,
       or_14_out, or_15_out, or_16_out, or_17_out, or_18_out;
  wire [15:0] add_1_s, multiplexer_2_out, multiplexer_3_out, sub_1_s, x;
  wire [31:0] multiplexer_1_out, multiplexer_4_out, multiplexer_5_out, multiplexer_8_out, multiplexer_9_out,
       multiplexer_10_out, multiplexer_11_out, multiplexer_12_out, multiplexer_13_out, multiplexer_14_out,
       multiplexer_15_out, multiplexer_16_out, multiplexer_17_out, multiplexer_18_out, multiplexer_19_out,
       multiplexer_20_out, x_R;
  wire [63:0] mul_1_mul, mul_2_mul, mul_3_mul, mul_4_mul, mul_5_mul, mul_6_mul, mul_7_mul, mul_8_mul,
       mul_9_mul, mul_10_mul, mul_11_mul, mul_12_mul, mul_13_mul, mul_14_mul, mul_15_mul;
  wire [63:32] mul_16_mul;

  Comparator #(.Bits(32)) comparator_1 (
    .a({{16{1'b0}}, A}), .b(x_R), .gt(comparator_1_gt), .eq(comparator_1_eq));  // open: lt
  Comparator #(.Bits(4)) comparator_2 (.a(R), .b(4'b0000), .gt(comparator_2_gt));  // open: eq, lt
  Comparator #(.Bits(32)) comparator_3 (
    .a(32'h1), .b({{16{1'b0}}, A}), .eq(comparator_3_eq), .lt(comparator_3_lt));  // open: gt
  Multiplexer #(.Bits(32)) multiplexer_1 (
    .sel(and_1_out), .in_0(32'h1), .in_1({{16{1'b0}}, x}), .out(multiplexer_1_out));
  and and_1 (and_1_out, comparator_2_gt, or_1_out);
  or or_1 (or_1_out, comparator_3_eq, comparator_3_lt);
  Add #(.Bits(16)) add_1 (.a(x), .b(16'h1), .c_i(1'b0), .s(add_1_s));  // open: c_o
  or or_2 (or_2_out, comparator_1_gt, comparator_1_eq);
  Mul #(.Bits(32)) mul_1 (.a(32'h1), .b(multiplexer_1_out), .mul(mul_1_mul));
  Multiplexer #(.Bits(16)) multiplexer_2 (.sel(or_2_out), .in_0(x), .in_1(add_1_s), .out(multiplexer_2_out));
  Comparator #(.Bits(4)) comparator_4 (.a(R), .b(4'b0001), .gt(comparator_4_gt));  // open: eq, lt
  Comparator #(.Bits(32)) comparator_5 (
    .a(mul_1_mul[31:0]), .b({{16{1'b0}}, A}), .eq(comparator_5_eq), .lt(comparator_5_lt));  // open: gt
  Multiplexer #(.Bits(16)) multiplexer_3 (
    .sel(\input ), .in_0(multiplexer_2_out), .in_1(16'h2), .out(multiplexer_3_out));
  or or_3 (or_3_out, \input , or_2_out);
  Multiplexer #(.Bits(32)) multiplexer_4 (
    .sel(and_2_out), .in_0(32'h1), .in_1({{16{1'b0}}, x}), .out(multiplexer_4_out));
  and and_2 (and_2_out, comparator_4_gt, or_4_out);
  or or_4 (or_4_out, comparator_5_eq, comparator_5_lt);
  Register #(.Bits(16)) register_1 (.D(multiplexer_3_out), .C(clk), .en(or_3_out), .Q(x));
  Mul #(.Bits(32)) mul_2 (.a(mul_1_mul[31:0]), .b(multiplexer_4_out), .mul(mul_2_mul));
  Comparator #(.Bits(4)) comparator_6 (.a(R), .b(4'b0010), .gt(comparator_6_gt));  // open: eq, lt
  Comparator #(.Bits(32)) comparator_7 (
    .a(mul_2_mul[31:0]), .b({{16{1'b0}}, A}), .eq(comparator_7_eq), .lt(comparator_7_lt));  // open: gt
  Sub #(.Bits(16)) sub_1 (.a(x), .b(16'h1), .c_i(1'b0), .s(sub_1_s));  // open: c_o
  Multiplexer #(.Bits(32)) multiplexer_5 (
    .sel(and_3_out), .in_0(32'h1), .in_1({{16{1'b0}}, x}), .out(multiplexer_5_out));
  and and_3 (and_3_out, comparator_6_gt, or_5_out);
  or or_5 (or_5_out, comparator_7_eq, comparator_7_lt);
  Comparator #(.Bits(4)) comparator_8 (.a(R), .b(4'b0001), .eq(comparator_8_eq));  // open: gt, lt
  Mul #(.Bits(32)) mul_3 (.a(mul_2_mul[31:0]), .b(multiplexer_5_out), .mul(mul_3_mul));
  Multiplexer #(.Bits(16)) multiplexer_6 (.sel(comparator_8_eq), .in_0(sub_1_s), .in_1(A), .out(nroot));
  Multiplexer multiplexer_7 (.sel(comparator_8_eq), .in_0(or_2_out), .in_1(1'b0), .out(busy));
  Comparator #(.Bits(4)) comparator_9 (.a(R), .b(4'b0011), .gt(comparator_9_gt));  // open: eq, lt
  Comparator #(.Bits(32)) comparator_10 (
    .a(mul_3_mul[31:0]), .b({{16{1'b0}}, A}), .eq(comparator_10_eq), .lt(comparator_10_lt));  // open: gt
  Multiplexer #(.Bits(32)) multiplexer_8 (
    .sel(and_4_out), .in_0(32'h1), .in_1({{16{1'b0}}, x}), .out(multiplexer_8_out));
  and and_4 (and_4_out, comparator_9_gt, or_6_out);
  or or_6 (or_6_out, comparator_10_eq, comparator_10_lt);
  Mul #(.Bits(32)) mul_4 (.a(mul_3_mul[31:0]), .b(multiplexer_8_out), .mul(mul_4_mul));
  Comparator #(.Bits(4)) comparator_11 (.a(R), .b(4'b0100), .gt(comparator_11_gt));  // open: eq, lt
  Comparator #(.Bits(32)) comparator_12 (
    .a(mul_4_mul[31:0]), .b({{16{1'b0}}, A}), .eq(comparator_12_eq), .lt(comparator_12_lt));  // open: gt
  Multiplexer #(.Bits(32)) multiplexer_9 (
    .sel(and_5_out), .in_0(32'h1), .in_1({{16{1'b0}}, x}), .out(multiplexer_9_out));
  and and_5 (and_5_out, comparator_11_gt, or_7_out);
  or or_7 (or_7_out, comparator_12_eq, comparator_12_lt);
  Mul #(.Bits(32)) mul_5 (.a(mul_4_mul[31:0]), .b(multiplexer_9_out), .mul(mul_5_mul));
  Comparator #(.Bits(4)) comparator_13 (.a(R), .b(4'b0101), .gt(comparator_13_gt));  // open: eq, lt
  Comparator #(.Bits(32)) comparator_14 (
    .a(mul_5_mul[31:0]), .b({{16{1'b0}}, A}), .eq(comparator_14_eq), .lt(comparator_14_lt));  // open: gt
  Multiplexer #(.Bits(32)) multiplexer_10 (
    .sel(and_6_out), .in_0(32'h1), .in_1({{16{1'b0}}, x}), .out(multiplexer_10_out));
  and and_6 (and_6_out, comparator_13_gt, or_8_out);
  or or_8 (or_8_out, comparator_14_eq, comparator_14_lt);
  Mul #(.Bits(32)) mul_6 (.a(mul_5_mul[31:0]), .b(multiplexer_10_out), .mul(mul_6_mul));
  Comparator #(.Bits(4)) comparator_15 (.a(R), .b(4'b0110), .gt(comparator_15_gt));  // open: eq, lt
  Comparator #(.Bits(32)) comparator_16 (
    .a(mul_6_mul[31:0]), .b({{16{1'b0}}, A}), .eq(comparator_16_eq), .lt(comparator_16_lt));  // open: gt
  Multiplexer #(.Bits(32)) multiplexer_11 (
    .sel(and_7_out), .in_0(32'h1), .in_1({{16{1'b0}}, x}), .out(multiplexer_11_out));
  and and_7 (and_7_out, comparator_15_gt, or_9_out);
  or or_9 (or_9_out, comparator_16_eq, comparator_16_lt);
  Mul #(.Bits(32)) mul_7 (.a(mul_6_mul[31:0]), .b(multiplexer_11_out), .mul(mul_7_mul));
  Comparator #(.Bits(4)) comparator_17 (.a(R), .b(4'b0111), .gt(comparator_17_gt));  // open: eq, lt
  Comparator #(.Bits(32)) comparator_18 (
    .a(mul_7_mul[31:0]), .b({{16{1'b0}}, A}), .eq(comparator_18_eq), .lt(comparator_18_lt));  // open: gt
  Multiplexer #(.Bits(32)) multiplexer_12 (
    .sel(and_8_out), .in_0(32'h1), .in_1({{16{1'b0}}, x}), .out(multiplexer_12_out));
  and and_8 (and_8_out, comparator_17_gt, or_10_out);
  or or_10 (or_10_out, comparator_18_eq, comparator_18_lt);
  Mul #(.Bits(32)) mul_8 (.a(mul_7_mul[31:0]), .b(multiplexer_12_out), .mul(mul_8_mul));
  Comparator #(.Bits(4)) comparator_19 (.a(R), .b(4'b1000), .gt(comparator_19_gt));  // open: eq, lt
  Comparator #(.Bits(32)) comparator_20 (
    .a(mul_8_mul[31:0]), .b({{16{1'b0}}, A}), .eq(comparator_20_eq), .lt(comparator_20_lt));  // open: gt
  Multiplexer #(.Bits(32)) multiplexer_13 (
    .sel(and_9_out), .in_0(32'h1), .in_1({{16{1'b0}}, x}), .out(multiplexer_13_out));
  and and_9 (and_9_out, comparator_19_gt, or_11_out);
  or or_11 (or_11_out, comparator_20_eq, comparator_20_lt);
  Mul #(.Bits(32)) mul_9 (.a(mul_8_mul[31:0]), .b(multiplexer_13_out), .mul(mul_9_mul));
  Comparator #(.Bits(4)) comparator_21 (.a(R), .b(4'b1001), .gt(comparator_21_gt));  // open: eq, lt
  Comparator #(.Bits(32)) comparator_22 (
    .a(mul_9_mul[31:0]), .b({{16{1'b0}}, A}), .eq(comparator_22_eq), .lt(comparator_22_lt));  // open: gt
  Multiplexer #(.Bits(32)) multiplexer_14 (
    .sel(and_10_out), .in_0(32'h1), .in_1({{16{1'b0}}, x}), .out(multiplexer_14_out));
  and and_10 (and_10_out, comparator_21_gt, or_12_out);
  or or_12 (or_12_out, comparator_22_eq, comparator_22_lt);
  Mul #(.Bits(32)) mul_10 (.a(mul_9_mul[31:0]), .b(multiplexer_14_out), .mul(mul_10_mul));
  Comparator #(.Bits(4)) comparator_23 (.a(R), .b(4'b1010), .gt(comparator_23_gt));  // open: eq, lt
  Comparator #(.Bits(32)) comparator_24 (
    .a(mul_10_mul[31:0]), .b({{16{1'b0}}, A}), .eq(comparator_24_eq), .lt(comparator_24_lt));  // open: gt
  Multiplexer #(.Bits(32)) multiplexer_15 (
    .sel(and_11_out), .in_0(32'h1), .in_1({{16{1'b0}}, x}), .out(multiplexer_15_out));
  and and_11 (and_11_out, comparator_23_gt, or_13_out);
  or or_13 (or_13_out, comparator_24_eq, comparator_24_lt);
  Mul #(.Bits(32)) mul_11 (.a(mul_10_mul[31:0]), .b(multiplexer_15_out), .mul(mul_11_mul));
  Comparator #(.Bits(4)) comparator_25 (.a(R), .b(4'b1011), .gt(comparator_25_gt));  // open: eq, lt
  Comparator #(.Bits(32)) comparator_26 (
    .a(mul_11_mul[31:0]), .b({{16{1'b0}}, A}), .eq(comparator_26_eq), .lt(comparator_26_lt));  // open: gt
  Multiplexer #(.Bits(32)) multiplexer_16 (
    .sel(and_12_out), .in_0(32'h1), .in_1({{16{1'b0}}, x}), .out(multiplexer_16_out));
  and and_12 (and_12_out, comparator_25_gt, or_14_out);
  or or_14 (or_14_out, comparator_26_eq, comparator_26_lt);
  Mul #(.Bits(32)) mul_12 (.a(mul_11_mul[31:0]), .b(multiplexer_16_out), .mul(mul_12_mul));
  Comparator #(.Bits(4)) comparator_27 (.a(R), .b(4'b1100), .gt(comparator_27_gt));  // open: eq, lt
  Comparator #(.Bits(32)) comparator_28 (
    .a(mul_12_mul[31:0]), .b({{16{1'b0}}, A}), .eq(comparator_28_eq), .lt(comparator_28_lt));  // open: gt
  Multiplexer #(.Bits(32)) multiplexer_17 (
    .sel(and_13_out), .in_0(32'h1), .in_1({{16{1'b0}}, x}), .out(multiplexer_17_out));
  and and_13 (and_13_out, comparator_27_gt, or_15_out);
  or or_15 (or_15_out, comparator_28_eq, comparator_28_lt);
  Mul #(.Bits(32)) mul_13 (.a(mul_12_mul[31:0]), .b(multiplexer_17_out), .mul(mul_13_mul));
  Comparator #(.Bits(4)) comparator_29 (.a(R), .b(4'b1101), .gt(comparator_29_gt));  // open: eq, lt
  Comparator #(.Bits(32)) comparator_30 (
    .a(mul_13_mul[31:0]), .b({{16{1'b0}}, A}), .eq(comparator_30_eq), .lt(comparator_30_lt));  // open: gt
  Multiplexer #(.Bits(32)) multiplexer_18 (
    .sel(and_14_out), .in_0(32'h1), .in_1({{16{1'b0}}, x}), .out(multiplexer_18_out));
  and and_14 (and_14_out, comparator_29_gt, or_16_out);
  or or_16 (or_16_out, comparator_30_eq, comparator_30_lt);
  Mul #(.Bits(32)) mul_14 (.a(mul_13_mul[31:0]), .b(multiplexer_18_out), .mul(mul_14_mul));
  Comparator #(.Bits(4)) comparator_31 (.a(R), .b(4'b1110), .gt(comparator_31_gt));  // open: eq, lt
  Comparator #(.Bits(32)) comparator_32 (
    .a(mul_14_mul[31:0]), .b({{16{1'b0}}, A}), .eq(comparator_32_eq), .lt(comparator_32_lt));  // open: gt
  Multiplexer #(.Bits(32)) multiplexer_19 (
    .sel(and_15_out), .in_0(32'h1), .in_1({{16{1'b0}}, x}), .out(multiplexer_19_out));
  and and_15 (and_15_out, comparator_31_gt, or_17_out);
  or or_17 (or_17_out, comparator_32_eq, comparator_32_lt);
  Mul #(.Bits(32)) mul_15 (.a(mul_14_mul[31:0]), .b(multiplexer_19_out), .mul(mul_15_mul));
  Comparator #(.Bits(4)) comparator_33 (.a(R), .b(4'b1111), .gt(comparator_33_gt));  // open: eq, lt
  Comparator #(.Bits(32)) comparator_34 (
    .a(mul_15_mul[31:0]), .b({{16{1'b0}}, A}), .eq(comparator_34_eq), .lt(comparator_34_lt));  // open: gt
  Multiplexer #(.Bits(32)) multiplexer_20 (
    .sel(and_16_out), .in_0(32'h1), .in_1({{16{1'b0}}, x}), .out(multiplexer_20_out));
  and and_16 (and_16_out, comparator_33_gt, or_18_out);
  or or_18 (or_18_out, comparator_34_eq, comparator_34_lt);
  Mul #(.Bits(32)) mul_16 (.a(mul_15_mul[31:0]), .b(multiplexer_20_out), .mul({mul_16_mul, x_R}));

  // Notes on the sheet:
  //   clk: Hz: 200
endmodule

/* Test case TestCase1:
clk A R input nroot busy
0 0 0 0 X 0
1 0 0 0 X 0
0 0 0 0 X 0
1 0 0 0 X 0
0 2 2 1 X X
1 2 2 1 X X
repeat (255) C 2 2 0 X X
0 2 2 0 1 0
1 2 2 0 1 0
0 0 0 0 X 0
1 0 0 0 X 0
0 0 0 0 X 0
1 0 0 0 X 0
0 4 2 1 X X
1 4 2 1 X X
repeat (255) C 4 2 0 X X
0 4 2 0 2 0
1 4 2 0 2 0
0 0 0 0 X 0
1 0 0 0 X 0
0 0 0 0 X 0
1 0 0 0 X 0
0 8 2 1 X X
1 8 2 1 X X
repeat (255) C 8 2 0 X X
0 8 2 0 2 0
1 8 2 0 2 0
0 0 0 0 X 0
1 0 0 0 X 0
0 0 0 0 X 0
1 0 0 0 X 0
0 16 2 1 X X
1 16 2 1 X X
repeat (255) C 16 2 0 X X
0 16 2 0 4 0
1 16 2 0 4 0
*/

/* Test case TestCase4:
clk A R input nroot busy
0 0 0 0 X 0
1 0 0 0 X 0
0 0 0 0 X 0
1 0 0 0 X 0
0 65530 12 1 X X
1 65530 12 1 X X
repeat (255) C 65530 12 0 X X
0 65530 12 0 2 0
1 65530 12 0 2 0
0 0 0 0 X 0
1 0 0 0 X 0
0 0 0 0 X 0
1 0 0 0 X 0
0 60000 3 1 X X
1 60000 3 1 X X
repeat (255) C 60000 3 0 X X
0 60000 3 0 39 0
1 60000 3 0 39 0
0 0 0 0 X 0
1 0 0 0 X 0
0 0 0 0 X 0
1 0 0 0 X 0
0 55124 4 1 X X
1 55124 4 1 X X
repeat (255) C 55124 4 0 X X
0 55124 4 0 15 0
1 55124 4 0 15 0
0 0 0 0 X 0
1 0 0 0 X 0
0 0 0 0 X 0
1 0 0 0 X 0
0 14778 5 1 X X
1 14778 5 1 X X
repeat (255) C 14778 5 0 X X
0 14778 5 0 6 0
1 14778 5 0 6 0
*/

/* Test case TestCase8:
clk A R input nroot busy
0 0 0 0 X 0
1 0 0 0 X 0
0 0 0 0 X 0
1 0 0 0 X 0
0 65535 1 1 X X
1 65535 1 1 X X
repeat (255) C 65535 1 0 X X
0 65535 1 0 65535 0
1 65535 1 0 65535 0
0 0 0 0 X 0
1 0 0 0 X 0
0 0 0 0 X 0
1 0 0 0 X 0
0 64000 15 1 X X
1 64000 15 1 X X
repeat (255) C 64000 15 0 X X
0 64000 15 0 2 0
1 64000 15 0 2 0
0 0 0 0 X 0
1 0 0 0 X 0
0 0 0 0 X 0
1 0 0 0 X 0
0 12000 5 1 X X
1 12000 5 1 X X
repeat (255) C 12000 5 0 X X
0 12000 5 0 6 0
1 12000 5 0 6 0
0 0 0 0 X 0
1 0 0 0 X 0
0 0 0 0 X 0
1 0 0 0 X 0
0 65535 15 1 X X
1 65535 15 1 X X
repeat (255) C 65535 15 0 X X
0 65535 15 0 2 0
1 65535 15 0 2 0
*/
