// Digital circuit Midterm_CP_2021_01_06.dig as structural Verilog
module Midterm_CP_2021_01_06 (
  input  A2,
  input  A1,
  input  A0,
  input  B2,
  input  B1,
  input  B0,
  output Output
);

  wire add_1_c_o, and_1_out, and_2_out, and_3_out, not_1_out, not_2_out, not_3_out, not_4_out;
  wire [2:0] add_1_s;

  not not_1 (not_1_out, add_1_c_o);
  not not_2 (not_2_out, add_1_s[2]);
  Add #(.Bits(3)) add_1 (.a({B2, B1, B0}), .b({A2, A1, A0}), .c_i(1'b0), .s(add_1_s), .c_o(add_1_c_o));
  not not_3 (not_3_out, add_1_s[1]);
  not not_4 (not_4_out, add_1_s[0]);
  and and_1 (and_1_out, not_1_out, not_2_out);
  and and_2 (and_2_out, not_1_out, not_3_out);
  and and_3 (and_3_out, not_1_out, not_4_out);
  or or_1 (Output, and_1_out, and_2_out, and_3_out);
  Seven_Seg seven_seg_1 (.a(Output), .b(1'b1), .c(1'b1), .d(Output), .e(Output), .f(Output), .g(1'b0), .dp(1'b0));
endmodule
