// Digital circuit Midterm_CP_2024_02.dig as structural Verilog
module Midterm_CP_2024_02 (
  input  [7:0] in,
  output [2:0] out
);

  wire or_1_out;
  wire [2:0] Left_num, multiplexer_1_out, Right_num, sub_1_s;

  PriorityEncoder #(.Selector_Bits(3)) Left (
    .in0(in[0]), .in1(in[1]), .in2(in[2]), .in3(in[3]), .in4(in[4]), .in5(in[5]), .in6(in[6]), .in7(in[7]),
    .num(Left_num));  // open: any
  PriorityEncoder #(.Selector_Bits(3)) Right (
    .in0(in[7]), .in1(in[6]), .in2(in[5]), .in3(in[4]), .in4(in[3]), .in5(in[2]), .in6(in[1]), .in7(in[0]),
    .num(Right_num));  // open: any
  or or_1 (or_1_out, in[0], in[1], in[2], in[3], in[4], in[5], in[6], in[7]);
  Sub #(.Bits(3)) sub_1 (.a(3'b111), .b(Right_num), .c_i(1'b0), .s(sub_1_s));  // open: c_o
  Multiplexer #(.Bits(3)) multiplexer_1 (.sel(or_1_out), .in_0(3'b000), .in_1(sub_1_s), .out(multiplexer_1_out));
  Sub #(.Bits(3)) sub_2 (.a(Left_num), .b(multiplexer_1_out), .c_i(1'b0), .s(out));  // open: c_o
endmodule
