// Digital circuit diglab_​02_​06.dig as structural Verilog
module diglab__02__06 (
  input  A,
  input  B,
  input  C,
  input  D,
  output Z1,
  output Z2,
  output Z3
);

  wire not_1_out, not_2_out, not_3_out, not_4_out, not_5_out, not_6_out, not_7_out, not_8_out, not_9_out,
       not_10_out, not_11_out, not_12_out, not_13_out, or_1_out, or_2_out, or_3_out, or_4_out, or_5_out,
       or_6_out, or_7_out, or_8_out, or_9_out, or_10_out, or_11_out, or_12_out, or_13_out, or_14_out;

  not not_1 (not_1_out, D);
  not not_2 (not_2_out, C);
  not not_3 (not_3_out, D);
  not not_4 (not_4_out, C);
  or or_1 (or_1_out, A, B);
  or or_2 (or_2_out, A, not_1_out);
  or or_3 (or_3_out, A, not_2_out);
  or or_4 (or_4_out, C, not_3_out);
  or or_5 (or_5_out, B, not_4_out);
  and and_1 (Z1, or_1_out, or_2_out, or_3_out, or_4_out, or_5_out);
  not not_5 (not_5_out, B);
  not not_6 (not_6_out, A);
  not not_7 (not_7_out, A);
  not not_8 (not_8_out, B);
  not not_9 (not_9_out, A);
  or or_6 (or_6_out, C, D);
  or or_7 (or_7_out, not_5_out, C);
  or or_8 (or_8_out, not_6_out, C);
  or or_9 (or_9_out, not_7_out, not_8_out);
  or or_10 (or_10_out, not_9_out, D);
  and and_2 (Z2, or_6_out, or_7_out, or_8_out, or_9_out, or_10_out);
  not not_10 (not_10_out, C);
  not not_11 (not_11_out, A);
  not not_12 (not_12_out, B);
  not not_13 (not_13_out, D);
  or or_11 (or_11_out, A, not_10_out);
  or or_12 (or_12_out, not_11_out, C);
  or or_13 (or_13_out, not_12_out, D);
  or or_14 (or_14_out, B, not_13_out);
  and and_3 (Z3, or_11_out, or_12_out, or_13_out, or_14_out);
endmodule
