// Digital circuit diglab_​02_​08.dig as structural Verilog
module diglab__02__08 (
  input  Selector,
  input  X0,
  input  X1,
  output Z
);

  wire not_1_out, or_1_out, or_2_out;

  not not_1 (not_1_out, Selector);
  or or_1 (or_1_out, Selector, X0);
  or or_2 (or_2_out, not_1_out, X1);
  and and_1 (Z, or_1_out, or_2_out);
endmodule
