// Digital circuit diglab_03_02.dig as structural Verilog
module diglab_03_02 (
  input  [2:0] In,
  input  A,
  input  B,
  input  D,
  input  clk,
  output C,
  output E,
  output F,
  output G,
  output H,
  output [7:0] Z
);

  wire and_1_out, and_2_out, and_3_out, and_4_out, and_5_out, and_6_out, and_7_out, and_8_out, and_9_out,
       and_10_out, and_11_out, and_12_out, and_13_out, and_14_out, and_15_out, not_1_out, not_2_out,
       not_3_out;

  not not_1 (not_1_out, In[2]);
  not not_2 (not_2_out, In[1]);
  not not_3 (not_3_out, In[0]);
  and and_1 (and_1_out, not_1_out, not_2_out, In[0]);
  and and_2 (and_2_out, In[2], In[1]);
  and and_3 (and_3_out, In[2], not_3_out);
  and and_4 (and_4_out, In[1], not_3_out);
  and and_5 (and_5_out, In[2], not_2_out);
  and and_6 (and_6_out, not_1_out, In[0]);
  and and_7 (and_7_out, In[2], not_2_out);
  and and_8 (and_8_out, not_1_out, In[1]);
  and and_9 (and_9_out, not_2_out, not_3_out);
  and and_10 (and_10_out, In[2], In[1], In[0]);
  and and_11 (and_11_out, In[2], not_2_out, not_3_out);
  and and_12 (and_12_out, not_1_out, In[1], not_3_out);
  and and_13 (and_13_out, not_1_out, not_2_out, In[0]);
  and and_14 (and_14_out, In[2], not_3_out);
  and and_15 (and_15_out, In[1], not_3_out);
  or or_1 (C, and_1_out, and_2_out, and_3_out, and_4_out);
  or or_2 (E, and_5_out, and_6_out);
  or or_3 (F, and_7_out, and_8_out, and_9_out);
  or or_4 (G, and_10_out, and_11_out, and_12_out);
  or or_5 (H, and_13_out, and_14_out, and_15_out);
  Terminal terminal_1 (.D({A, B, C, D, E, F, G, H}), .C(clk), .en(1'b1));

  assign Z = {A, B, C, D, E, F, G, H};

  // Other names for the same wires on the sheet: X0 = In[0]; X1 = In[1]; X2 = In[2]

  // Notes on the sheet:
  //   B: default 1
endmodule
