// Digital circuit diglab_03_04.dig as structural Verilog
module diglab_03_04 (
  input  [6:0] In,
  output [6:0] Output
);

  wire B1, B2, B3, B4, B5, B6, B7, C1, C2, C3, not_1_out, not_2_out, not_3_out;

  assign Output = {B1, B2, B3, B4, B5, B6, B7} ^ In;  // XOr xor_1, 7 bits wide
  xor xor_2 (C1, In[3], In[2], In[1], In[0]);
  xor xor_3 (C2, In[5], In[4], In[1], In[0]);
  xor xor_4 (C3, In[6], In[4], In[2], In[0]);
  not not_1 (not_1_out, C1);
  not not_2 (not_2_out, C2);
  not not_3 (not_3_out, C3);
  and and_1 (B1, not_1_out, not_2_out, C3);
  and and_2 (B2, not_1_out, C2, not_3_out);
  and and_3 (B3, not_1_out, C2, C3);
  and and_4 (B4, C1, not_2_out, not_3_out);
  and and_5 (B5, C1, not_2_out, C3);
  and and_6 (B6, C1, C2, not_3_out);
  and and_7 (B7, C1, C2, C3);

  // Other names for the same wires on the sheet: M4 = In[0]; M3 = In[1]; M2 = In[2]; P3 = In[3]; M1 = In[4];
  //   P2 = In[5]; P1 = In[6]
endmodule
