// Digital circuit Full_Adder_7400.dig as structural Verilog
module Full_Adder_7400 (
  input  A,
  input  B,
  input  Cin,
  output Cout,
  output Sum
);

  wire _7400_1_pin3, _7400_1_pin4, _7400_1_pin5, _7400_1_pin6, _7400_2_pin3, _7400_2_pin6, _7400_3_pin3;

  _7400 _7400_1 (
    .pin1(A), .pin2(B), .pin3(_7400_1_pin3), .pin4(_7400_1_pin4), .pin5(_7400_1_pin5), .pin6(_7400_1_pin6),
    .pin7(1'b0), .pin8(_7400_1_pin5), .pin9(B), .pin10(_7400_1_pin3), .pin11(_7400_1_pin4),
    .pin12(_7400_1_pin3), .pin13(A), .pin14(1'b1));
  _7400 _7400_2 (
    .pin1(_7400_1_pin6), .pin2(Cin), .pin3(_7400_2_pin3), .pin4(_7400_2_pin3), .pin5(_7400_1_pin6),
    .pin6(_7400_2_pin6), .pin7(1'b0), .pin9(1'b0), .pin10(1'b0), .pin12(1'b0), .pin13(1'b0), .pin14(1'b1));  // open: pin8, pin11
  _7400 _7400_3 (
    .pin1(_7400_2_pin3), .pin2(Cin), .pin3(_7400_3_pin3), .pin4(_7400_2_pin6), .pin5(_7400_3_pin3),
    .pin6(Sum), .pin7(1'b0), .pin9(1'b0), .pin10(1'b0), .pin11(Cout), .pin12(_7400_1_pin3),
    .pin13(_7400_2_pin3), .pin14(1'b1));  // open: pin8
endmodule
