// Digital circuit Half_Adder_NAND.dig as structural Verilog
module Half_Adder_NAND (
  input  A,
  input  B,
  output Sum,
  output Cout
);

  wire nand_1_out, nand_2_out, nand_3_out;

  nand nand_1 (nand_1_out, A, B);
  nand nand_2 (nand_2_out, A, nand_1_out);
  nand nand_3 (nand_3_out, nand_1_out, B);
  nand nand_4 (Sum, nand_2_out, nand_3_out);
  nand nand_5 (Cout, nand_1_out, nand_1_out);
endmodule
