// Digital circuit Half_Adder_SOP.dig as structural Verilog
module Half_Adder_SOP (
  input  A,
  input  B,
  output Sum,
  output Cout
);

  wire and_1_out, and_2_out, not_1_out, not_2_out;

  not not_1 (not_1_out, A);
  not not_2 (not_2_out, B);
  and and_1 (and_1_out, not_1_out, B);
  and and_2 (and_2_out, A, not_2_out);
  and and_3 (Cout, A, B);
  or or_1 (Sum, and_1_out, and_2_out);
endmodule
