// Digital circuit Half_Adder_toNAND01.dig as structural Verilog
module Half_Adder_toNAND01 (
  input  A,
  input  B,
  output Sum
);

  wire and_1_out, and_2_out;

  and and_1 (and_1_out, ~A, B);  // And
  and and_2 (and_2_out, A, ~B);  // And
  or or_1 (Sum, and_1_out, and_2_out);
endmodule
