// Digital circuit Half_Adder_toNAND02.dig as structural Verilog
module Half_Adder_toNAND02 (
  input  A,
  input  B,
  output Sum
);

  wire nand_1_out, nand_2_out;

  nand nand_1 (nand_1_out, ~A, B);  // NAnd
  nand nand_2 (nand_2_out, A, ~B);  // NAnd
  or or_1 (Sum, ~nand_1_out, ~nand_2_out);  // Or
endmodule
