// Digital circuit Full_Adder_7400.dig as structural Verilog
module Full_Adder_7400 (
  input  A,
  input  B,
  input  Cin,
  output Sum,
  output Cout
);

  wire _7400_1_pin3, _7400_1_pin6, _7400_1_pin8, _7400_1_pin10, _7400_2_pin8, _7400_2_pin10, _7400_3_pin10;

  _7400 _7400_1 (
    .pin1(A), .pin2(B), .pin3(_7400_1_pin3), .pin4(_7400_1_pin3), .pin5(A), .pin6(_7400_1_pin6), .pin7(1'b0),
    .pin8(_7400_1_pin8), .pin9(_7400_1_pin6), .pin10(_7400_1_pin10), .pin11(_7400_1_pin10), .pin12(B),
    .pin13(_7400_1_pin3), .pin14(1'b1));
  _7400 _7400_2 (
    .pin1(1'b0), .pin2(1'b0), .pin4(1'b0), .pin5(1'b0), .pin7(1'b0), .pin8(_7400_2_pin8),
    .pin9(_7400_1_pin8), .pin10(_7400_2_pin10), .pin11(_7400_2_pin10), .pin12(Cin), .pin13(_7400_1_pin8),
    .pin14(1'b1));  // open: pin3, pin6
  _7400 _7400_3 (
    .pin1(_7400_2_pin10), .pin2(_7400_1_pin3), .pin3(Cout), .pin4(1'b0), .pin5(1'b0), .pin7(1'b0),
    .pin8(Sum), .pin9(_7400_2_pin8), .pin10(_7400_3_pin10), .pin11(_7400_3_pin10), .pin12(Cin),
    .pin13(_7400_2_pin10), .pin14(1'b1));  // open: pin6
endmodule
