// Digital circuit Full_Adder_toNAND01.dig as structural Verilog
module Full_Adder_toNAND01 (
  input  A,
  input  B,
  input  Cin,
  output Sum
);

  wire xor_1_out;

  xor xor_1 (xor_1_out, A, B);
  xor xor_2 (Sum, xor_1_out, Cin);
endmodule
