// Digital circuit Template.dig as structural Verilog
module Template (
  input  A,
  input  B,
  input  C,
  input  D,
  output Before
);

  wire and_1_out, and_2_out;

  and and_1 (and_1_out, ~C, D);  // And
  and and_2 (and_2_out, A, ~B, D);  // And
  or or_1 (Before, and_1_out, ~A, and_2_out);  // Or
endmodule

/* Test case T1:
A B C D Before
0 0 1 1 1
1 0 1 1 1
1 0 1 1 1
*/
