// Digital circuit diglab_05_02.dig as structural Verilog
module diglab_05_02 (
  input  A,
  input  B,
  input  C,
  input  D,
  input  E,
  output Before,
  output After
);

  wire and_1_out, and_2_out, and_3_out, and_4_out, and_5_out, and_6_out, and_7_out, and_8_out, not_1_out,
       not_2_out, not_3_out, not_4_out, not_5_out, not_6_out, not_7_out, not_8_out, not_9_out, not_10_out;

  not not_1 (not_1_out, A);
  not not_2 (not_2_out, A);
  not not_3 (not_3_out, B);
  not not_4 (not_4_out, B);
  not not_5 (not_5_out, C);
  not not_6 (not_6_out, C);
  not not_7 (not_7_out, D);
  not not_8 (not_8_out, D);
  not not_9 (not_9_out, E);
  not not_10 (not_10_out, E);
  and and_1 (and_1_out, C, not_7_out, not_9_out);
  and and_2 (and_2_out, not_3_out, not_5_out, not_7_out);
  and and_3 (and_3_out, not_1_out, D, E);
  and and_4 (and_4_out, C, not_8_out, not_10_out);
  and and_5 (and_5_out, not_4_out, not_6_out, not_8_out);
  and and_6 (and_6_out, not_2_out, D, E);
  and and_7 (and_7_out, not_4_out, not_8_out, not_10_out);
  and and_8 (and_8_out, not_2_out, not_4_out, not_6_out, E);
  or or_1 (Before, and_1_out, and_2_out, and_3_out);
  or or_2 (After, and_4_out, and_5_out, and_6_out, and_7_out, and_8_out);
endmodule

/* Test case test1:
A B C D E Before After
0 0 0 0 0 1 1
0 0 1 0 0 1 1
0 0 0 0 0 1 1
0 0 1 0 0 1 1
0 0 0 0 0 1 1
0 0 1 0 0 1 1
0 0 0 0 0 1 1
0 0 1 0 0 1 1
*/

/* Test case test2:
A B C D E Before After
0 0 0 0 1 1 1
0 0 0 1 1 1 1
0 0 0 0 1 1 1
0 0 0 1 1 1 1
0 0 0 0 1 1 1
0 0 0 1 1 1 1
0 0 0 0 1 1 1
0 0 0 1 1 1 1
*/

/* Test case test3:
A B C D E Before After
1 0 0 0 0 1 1
1 0 1 0 0 1 1
1 0 0 0 0 1 1
1 0 1 0 0 1 1
1 0 0 0 0 1 1
1 0 1 0 0 1 1
1 0 0 0 0 1 1
1 0 1 0 0 1 1
*/
