// Digital circuit diglab_06_01_arithmetic01.dig as structural Verilog
module diglab_06_01_arithmetic01 (
  input  [3:0] A,
  input  [3:0] B,
  input  [2:0] S,
  input  C
);

  wire [3:0] A_1_plus_C_2_s, A_1_plus_C_s, A_B_1_plus_C_s, A_plus_B_plus_C_s, A_plus_C_s, B_plus_C_s,
       not_1_out, not_2_out;

  assign not_1_out = ~B;  // Not not_1, 4 bits wide
  assign not_2_out = ~A;  // Not not_2, 4 bits wide
  Add #(.Bits(4)) A_plus_C (.a(A), .b(4'b0000), .c_i(C), .s(A_plus_C_s));  // open: c_o
  Add #(.Bits(4)) A_1_plus_C (.a(A), .b(4'b1111), .c_i(C), .s(A_1_plus_C_s));  // open: c_o
  Add #(.Bits(4)) A_plus_B_plus_C (.a(A), .b(B), .c_i(C), .s(A_plus_B_plus_C_s));  // open: c_o
  Add #(.Bits(4)) A_B_1_plus_C (.a(A), .b(not_1_out), .c_i(C), .s(A_B_1_plus_C_s));  // open: c_o
  Add #(.Bits(4)) A_1_plus_C_2 (.a(not_2_out), .b(4'b0000), .c_i(C), .s(A_1_plus_C_2_s));  // open: c_o
  Add #(.Bits(4)) B_plus_C (.a(4'b0000), .b(B), .c_i(C), .s(B_plus_C_s));  // open: c_o
endmodule
