// Digital circuit diglab_06_01_logic01.dig as structural Verilog
module diglab_06_01_logic01 (
  input  [3:0] A,
  input  [3:0] B,
  input  [2:0] S
);

  wire [3:0] and_1_out, and_2_out, nand_1_out, nor_1_out, not_1_out, not_2_out, or_1_out, xnor_1_out;

  assign not_1_out = ~A;  // Not not_1, 4 bits wide
  assign nand_1_out = ~(A & B);  // NAnd nand_1, 4 bits wide
  assign nor_1_out = ~(A | B);  // NOr nor_1, 4 bits wide
  assign xnor_1_out = ~(A ^ B);  // XNOr xnor_1, 4 bits wide
  assign and_1_out = A & B;  // And and_1, 4 bits wide
  assign or_1_out = A | B;  // Or or_1, 4 bits wide
  assign not_2_out = ~B;  // Not not_2, 4 bits wide
  assign and_2_out = A & not_2_out;  // And and_2, 4 bits wide
endmodule
