// Digital circuit diglab_07_01_driver01.dig as structural Verilog
module diglab_07_01_driver01 (
  input  In,
  input  OE,
  output Out
);

  assign Out = OE ? In : 1'bz;  // Driver driver_1
endmodule
