// Digital circuit diglab_07_01_driver02.dig as structural Verilog
module diglab_07_01_driver02 (
  input  In,
  input  OE,
  output Out
);

  assign Out = ~OE ? In : 1'bz;  // DriverInvSel driverinvsel_1
endmodule
