// Digital circuit diglab_07_03_JK_MS.dig as structural Verilog
module diglab_07_03_JK_MS (
  input  J,
  input  Clock,
  input  K,
  output Q,
  output Q_2
);

  wire and_1_out, and_2_out, and_3_out, and_4_out, nor_1_out, nor_2_out, not_1_out;

  and and_1 (and_1_out, Q_2, J, Clock);
  and and_2 (and_2_out, Clock, K, Q);
  not not_1 (not_1_out, Clock);
  nor nor_1 (nor_1_out, and_1_out, nor_2_out);
  nor nor_2 (nor_2_out, nor_1_out, and_2_out);
  and and_3 (and_3_out, nor_1_out, not_1_out);
  and and_4 (and_4_out, not_1_out, nor_2_out);
  nor nor_3 (Q, and_3_out, Q_2);
  nor nor_4 (Q_2, Q, and_4_out);

  // Notes on the sheet:
  //   Master Stage
  //   S
  //   R
  //   Slave Stage
  //   \P
  //   P
endmodule
