// Digital circuit diglab_07_04_DNeg.dig as structural Verilog
module diglab_07_04_DNeg (
  input  Clock,
  input  D,
  output Q,
  output Q_2
);

  wire nor_1_out, nor_2_out, nor_3_out, nor_4_out;

  nor nor_1 (nor_1_out, nor_4_out, nor_2_out);
  nor nor_2 (nor_2_out, nor_1_out, Clock);
  nor nor_3 (nor_3_out, nor_2_out, Clock, nor_4_out);
  nor nor_4 (nor_4_out, nor_3_out, D);
  nor nor_5 (Q_2, nor_2_out, Q);
  nor nor_6 (Q, Q_2, nor_3_out);
endmodule
