// Digital circuit diglab_07_05.dig as structural Verilog
module diglab_07_05 (
  input  Clock,
  input  T,
  input  Clear,
  output Q,
  output Q_2
);

  wire and_1_out, nor_1_out, nor_2_out, nor_3_out, nor_4_out, not_1_out, not_2_out, xor_1_out;

  not not_1 (not_1_out, Clear);
  xor xor_1 (xor_1_out, T, Q_2);
  not not_2 (not_2_out, Clock);
  and and_1 (and_1_out, not_1_out, xor_1_out);
  nor nor_1 (nor_1_out, nor_4_out, nor_2_out);
  nor nor_2 (nor_2_out, nor_1_out, not_2_out);
  nor nor_3 (nor_3_out, nor_2_out, not_2_out, nor_4_out);
  nor nor_4 (nor_4_out, nor_3_out, and_1_out);
  nor nor_5 (Q_2, nor_2_out, Q);
  nor nor_6 (Q, Q_2, nor_3_out);
endmodule
