// Digital circuit diglab_08_01_adder.dig as structural Verilog
module diglab_08_01_adder (
  input  Clock,
  input  D,
  input  C,
  input  B,
  input  A,
  input  Load,
  output QD,
  output QC,
  output QB,
  output QA,
  output RCO
);

  wire [3:0] Add_1_s, multiplexer_1_out;

  Add #(.Bits(4)) Add_1 (.a({QD, QC, QB, QA}), .b(4'b0000), .c_i(1'b1), .s(Add_1_s), .c_o(RCO));
  Multiplexer #(.Bits(4)) multiplexer_1 (.sel(Load), .in_0({D, C, B, A}), .in_1(Add_1_s), .out(multiplexer_1_out));
  D_FF #(.Bits(4)) d_ff_1 (.D(multiplexer_1_out), .C(Clock), .Q({QD, QC, QB, QA}));  // open: nQ
endmodule
