// Digital circuit diglab_08_01_adderEnable.dig as structural Verilog
module diglab_08_01_adderEnable (
  input  Clock,
  input  D,
  input  C,
  input  B,
  input  A,
  input  Load,
  input  P,
  input  T,
  output QD,
  output QC,
  output QB,
  output QA,
  output RCO
);

  wire and_1_out;
  wire [3:0] Add_1_s, multiplexer_1_out, multiplexer_2_out;

  Add #(.Bits(4)) Add_1 (.a({QD, QC, QB, QA}), .b(4'b0000), .c_i(1'b1), .s(Add_1_s), .c_o(RCO));
  and and_1 (and_1_out, P, T);
  Multiplexer multiplexer_1 (.sel(and_1_out), .in_0(A), .in_1(Add_1_s[0]), .out(multiplexer_1_out[0]));
  Multiplexer #(.Bits(4)) multiplexer_2 (
    .sel(Load), .in_0({D, C, B, A}), .in_1(multiplexer_1_out), .out(multiplexer_2_out));
  D_FF #(.Bits(4)) d_ff_1 (.D(multiplexer_2_out), .C(Clock), .Q({QD, QC, QB, QA}));  // open: nQ
  // Pins of 1 and 4 bits meet at {D, C, B, A}
  // Pins of 1 and 4 bits meet at multiplexer_1_out
  // Pins of 1 and 4 bits meet at Add_1_s
endmodule
