// Digital circuit diglab_08_01_memory.dig as structural Verilog
module diglab_08_01_memory (
  input  Clock,
  input  D,
  input  C,
  input  B,
  input  A,
  input  Load,
  output QD,
  output QC,
  output QB,
  output QA
);

  wire [3:0] multiplexer_1_out;

  Multiplexer #(.Bits(4)) multiplexer_1 (.sel(Load), .in_0({D, C, B, A}), .out(multiplexer_1_out));  // open: in_1
  D_FF #(.Bits(4)) d_ff_1 (.D(multiplexer_1_out), .C(Clock), .Q({QD, QC, QB, QA}));  // open: nQ
endmodule
