// Digital circuit diglab_08_02_adder.dig as structural Verilog
module diglab_08_02_adder (
  input  A,
  input  B,
  input  Clock,
  output Z
);

  wire add_1_c_o, d_ff_1_q;

  Add add_1 (.a(A), .b(B), .c_i(d_ff_1_q), .s(Z), .c_o(add_1_c_o));
  D_FF d_ff_1 (.D(add_1_c_o), .C(Clock), .Q(d_ff_1_q));  // open: nQ
endmodule
