// Digital circuit diglab_08_03_delay.dig as structural Verilog
module diglab_08_03_delay (
  input  P,
  input  clock,
  output Z
);

  wire d_ff_1_nq;

  D_FF d_ff_1 (.D(P), .C(clock), .nQ(d_ff_1_nq));  // open: Q
  and and_1 (Z, P, d_ff_1_nq);
endmodule
