// Digital circuit diglab_08_03_moreDelay.dig as structural Verilog
module diglab_08_03_moreDelay (
  input  P,
  input  clock,
  output Z
);

  wire and_1_out, d_ff_1_nq;

  D_FF d_ff_1 (.D(P), .C(clock), .nQ(d_ff_1_nq));  // open: Q
  and and_1 (and_1_out, P, d_ff_1_nq);
  D_FF d_ff_2 (.D(and_1_out), .C(clock), .Q(Z));  // open: nQ
endmodule
