// Digital circuit diglab_08_03_pulser.dig as structural Verilog
module diglab_08_03_pulser (
  input  Input,
  input  Clock,
  output Output
);

  wire d_ff_1_nq, d_ff_2_q, d_ff_3_q;

  D_FF d_ff_1 (.D(Input), .C(Clock), .nQ(d_ff_1_nq));  // open: Q
  D_FF d_ff_2 (.D(Input), .C(Clock), .Q(d_ff_2_q));  // open: nQ
  D_FF d_ff_3 (.D(d_ff_1_nq), .C(Clock), .Q(d_ff_3_q));  // open: nQ
  and and_1 (Output, d_ff_2_q, d_ff_3_q);
endmodule
