// Digital circuit diglab_08_04.dig as structural Verilog
module diglab_08_04 (
  input  P,
  input  clock,
  input  Clr,
  output Z
);

  wire and_1_out, d_ff_1_q, d_ff_2_q, multiplexer_1_out, xor_1_out;

  and and_1 (and_1_out, P, ~Clr);  // And
  D_FF d_ff_1 (.D(and_1_out), .C(clock), .Q(d_ff_1_q));  // open: nQ
  D_FF d_ff_2 (.D(d_ff_1_q), .C(clock), .Q(d_ff_2_q));  // open: nQ
  xor xor_1 (xor_1_out, d_ff_1_q, d_ff_2_q);
  D_FF d_ff_3 (.D(multiplexer_1_out), .C(clock), .Q(Z));  // open: nQ
  Multiplexer multiplexer_1 (.sel(d_ff_1_q), .in_0(1'b0), .in_1(xor_1_out), .out(multiplexer_1_out));
endmodule
