// Digital circuit diglab_08_05.dig as structural Verilog
module diglab_08_05 (
  input  P,
  input  Clr,
  input  clock,
  output Z
);

  wire and_1_out, and_2_out, d_ff_1_q, d_ff_2_nq;

  and and_1 (and_1_out, P, ~Clr);  // And
  and and_2 (and_2_out, and_1_out, d_ff_1_q);
  D_FF d_ff_1 (.D(and_1_out), .C(clock), .Q(d_ff_1_q));  // open: nQ
  D_FF d_ff_2 (.D(and_2_out), .C(clock), .nQ(d_ff_2_nq));  // open: Q
  and and_3 (Z, d_ff_1_q, d_ff_2_nq);
endmodule
