// Digital circuit diglab_08_05_Dflipflop.dig as structural Verilog
module diglab_08_05_Dflipflop (
  input  P,
  input  clock,
  output Z
);

  D_FF d_ff_1 (.D(P), .C(clock), .nQ(Z));  // open: Q
endmodule
