// Digital circuit diglab_08_05_delay.dig as structural Verilog
module diglab_08_05_delay (
  input  P,
  input  clock,
  output Z
);

  wire d_ff_1_nq;

  D_FF d_ff_1 (.D(P), .C(clock), .nQ(d_ff_1_nq));  // open: Q
  D_FF d_ff_2 (.D(d_ff_1_nq), .C(clock), .Q(Z));  // open: nQ
endmodule
