// Digital circuit diglab_08_05_realMoreDelay.dig as structural Verilog
module diglab_08_05_realMoreDelay (
  input  P,
  input  clock,
  output Z
);

  wire d_ff_1_nq, d_ff_2_q, d_ff_3_q;

  D_FF d_ff_1 (.D(P), .C(clock), .nQ(d_ff_1_nq));  // open: Q
  D_FF d_ff_2 (.D(P), .C(clock), .Q(d_ff_2_q));  // open: nQ
  D_FF d_ff_3 (.D(d_ff_1_nq), .C(clock), .Q(d_ff_3_q));  // open: nQ
  and and_1 (Z, d_ff_2_q, d_ff_3_q);
endmodule
