// Digital circuit diglab_09_01.dig as structural Verilog
module diglab_09_01 (
  input  P5,
  input  reset,
  input  clock,
  input  P10,
  input  P20,
  input  Pcoffee,
  input  Ptea,
  input  Pchange,
  input  Pnext,
  output [5:0] Balance,
  output TeaOut,
  output CoffeeOut,
  output [1:0] Change5,
  output [1:0] Change10,
  output [1:0] Change20
);

  wire Add5, Add10, Add20, and_1_out, and_2_out, and_3_out, and_4_out, and_5_out, BuyCoffee, BuyTea,
       CHANGE_q, Coffee_2_q, Coffee_gt, d_ff_1_nq, d_ff_2_nq, d_ff_3_nq, d_ff_4_nq, d_ff_5_nq, d_ff_6_q,
       d_ff_7_q, d_ff_8_q, d_ff_9_q, d_ff_10_q, d_ff_11_q, d_ff_12_q, d_ff_13_q, d_ff_14_q, d_ff_15_q,
       d_ff_16_nq, d_ff_17_nq, d_ff_18_q, d_ff_19_q, d_ff_22_q, d_ff_23_q, MoneyChange, NEXT_q, NextDrink,
       not_1_out, not_2_out, not_3_out, not_4_out, not_5_out, not_6_out, not_7_out, not_8_out, not_9_out,
       not_10_out, or_1_out, or_2_out, or_3_out, P5_lt, P10_lt, P20_lt, Tea_2_q, Tea_gt;
  wire [5:0] ADD_s, BUY_s, C5_q, C10_q, C10_r, C20_q, C20_r, d_ff_24_q, multiplexer_1_out, multiplexer_2_out,
       multiplexer_3_out, multiplexer_5_out, multiplexer_6_out, multiplexer_7_out;
  wire [5:2] d_ff_25_q, d_ff_26_q, d_ff_27_q;

  Comparator #(.Bits(6)) u_P5 (.a(Balance), .b(6'b101110), .lt(P5_lt));  // open: gt, eq
  Comparator #(.Bits(6)) u_P10 (.a(Balance), .b(6'b101001), .lt(P10_lt));  // open: gt, eq
  Comparator #(.Bits(6)) u_P20 (.a(Balance), .b(6'b011111), .lt(P20_lt));  // open: gt, eq
  Comparator #(.Bits(6)) Tea (.a(Balance), .b(6'b010011), .gt(Tea_gt));  // open: eq, lt
  Comparator #(.Bits(6)) Coffee (.a(Balance), .b(6'b011000), .gt(Coffee_gt));  // open: eq, lt
  and and_1 (and_1_out, P5_lt, P5, not_1_out, not_2_out);
  not not_1 (not_1_out, CoffeeOut);
  not not_2 (not_2_out, TeaOut);
  and and_2 (and_2_out, P10_lt, P10, not_3_out, not_4_out);
  not not_3 (not_3_out, CoffeeOut);
  not not_4 (not_4_out, TeaOut);
  and and_3 (and_3_out, P20_lt, P20, not_5_out, not_6_out);
  not not_5 (not_5_out, CoffeeOut);
  not not_6 (not_6_out, TeaOut);
  and and_4 (and_4_out, Tea_gt, Ptea, not_7_out, not_8_out);
  not not_7 (not_7_out, CoffeeOut);
  not not_8 (not_8_out, TeaOut);
  and and_5 (and_5_out, Coffee_gt, Pcoffee, not_9_out, not_10_out);
  not not_9 (not_9_out, CoffeeOut);
  not not_10 (not_10_out, TeaOut);
  D_FF d_ff_1 (.D(and_1_out), .C(clock), .nQ(d_ff_1_nq));  // open: Q
  D_FF d_ff_2 (.D(and_2_out), .C(clock), .nQ(d_ff_2_nq));  // open: Q
  D_FF d_ff_3 (.D(and_3_out), .C(clock), .nQ(d_ff_3_nq));  // open: Q
  D_FF d_ff_4 (.D(and_4_out), .C(clock), .nQ(d_ff_4_nq));  // open: Q
  D_FF d_ff_5 (.D(and_5_out), .C(clock), .nQ(d_ff_5_nq));  // open: Q
  D_FF d_ff_6 (.D(and_1_out), .C(clock), .Q(d_ff_6_q));  // open: nQ
  D_FF d_ff_7 (.D(d_ff_1_nq), .C(clock), .Q(d_ff_7_q));  // open: nQ
  D_FF d_ff_8 (.D(and_2_out), .C(clock), .Q(d_ff_8_q));  // open: nQ
  D_FF d_ff_9 (.D(d_ff_2_nq), .C(clock), .Q(d_ff_9_q));  // open: nQ
  D_FF d_ff_10 (.D(and_3_out), .C(clock), .Q(d_ff_10_q));  // open: nQ
  D_FF d_ff_11 (.D(d_ff_3_nq), .C(clock), .Q(d_ff_11_q));  // open: nQ
  D_FF d_ff_12 (.D(and_4_out), .C(clock), .Q(d_ff_12_q));  // open: nQ
  D_FF d_ff_13 (.D(d_ff_4_nq), .C(clock), .Q(d_ff_13_q));  // open: nQ
  D_FF d_ff_14 (.D(and_5_out), .C(clock), .Q(d_ff_14_q));  // open: nQ
  D_FF d_ff_15 (.D(d_ff_5_nq), .C(clock), .Q(d_ff_15_q));  // open: nQ
  and and_6 (Add5, d_ff_6_q, d_ff_7_q);
  and and_7 (Add10, d_ff_8_q, d_ff_9_q);
  and and_8 (Add20, d_ff_10_q, d_ff_11_q);
  and and_9 (BuyTea, d_ff_12_q, d_ff_13_q);
  and and_10 (BuyCoffee, d_ff_14_q, d_ff_15_q);
  Multiplexer #(.Selector_Bits(3), .Bits(6)) multiplexer_1 (
    .sel({Add20, Add10, Add5}), .in_0({6{1'b0}}), .in_1(6'b000101), .in_2(6'b001010), .in_3({6{1'b0}}),
    .in_4(6'b010100), .in_5({6{1'b0}}), .in_6({6{1'b0}}), .in_7({6{1'b0}}), .out(multiplexer_1_out));
  Multiplexer #(.Selector_Bits(2), .Bits(6)) multiplexer_2 (
    .sel({BuyCoffee, BuyTea}), .in_0({6{1'b0}}), .in_1(6'b010100), .in_2(6'b011001), .in_3({6{1'b0}}),
    .out(multiplexer_2_out));
  or or_1 (or_1_out, reset, NextDrink, MoneyChange);
  D_FF NEXT (.D(Pnext), .C(clock), .Q(NEXT_q));  // open: nQ
  D_FF CHANGE (.D(Pchange), .C(clock), .Q(CHANGE_q));  // open: nQ
  D_FF d_ff_16 (.D(NEXT_q), .C(clock), .nQ(d_ff_16_nq));  // open: Q
  D_FF d_ff_17 (.D(CHANGE_q), .C(clock), .nQ(d_ff_17_nq));  // open: Q
  Add #(.Bits(6)) ADD (.a(Balance), .b(multiplexer_1_out), .c_i(1'b0), .s(ADD_s));  // open: c_o
  Sub #(.Bits(6)) BUY (.a(Balance), .b(multiplexer_2_out), .c_i(1'b0), .s(BUY_s));  // open: c_o
  or or_2 (or_2_out, BuyTea, BuyCoffee);
  RS_FF_AS Tea_2 (.S(BuyTea), .R(or_1_out), .Q(Tea_2_q));  // open: nQ
  RS_FF_AS Coffee_2 (.S(BuyCoffee), .R(or_1_out), .Q(Coffee_2_q));  // open: nQ
  Multiplexer #(.Bits(6)) multiplexer_3 (.sel(or_2_out), .in_0(ADD_s), .in_1(BUY_s), .out(multiplexer_3_out));
  D_FF d_ff_18 (.D(NEXT_q), .C(clock), .Q(d_ff_18_q));  // open: nQ
  D_FF d_ff_19 (.D(d_ff_16_nq), .C(clock), .Q(d_ff_19_q));  // open: nQ
  D_FF d_ff_20 (.D(Tea_2_q), .C(clock), .Q(TeaOut));  // open: nQ
  D_FF d_ff_21 (.D(Coffee_2_q), .C(clock), .Q(CoffeeOut));  // open: nQ
  D_FF d_ff_22 (.D(CHANGE_q), .C(clock), .Q(d_ff_22_q));  // open: nQ
  D_FF d_ff_23 (.D(d_ff_17_nq), .C(clock), .Q(d_ff_23_q));  // open: nQ
  D_FF #(.Bits(6)) d_ff_24 (.D(multiplexer_3_out), .C(clock), .Q(d_ff_24_q));  // open: nQ
  and and_11 (NextDrink, d_ff_18_q, d_ff_19_q);
  and and_12 (MoneyChange, d_ff_22_q, d_ff_23_q);
  or or_3 (or_3_out, MoneyChange, reset);
  Multiplexer #(.Bits(6)) multiplexer_4 (.sel(or_3_out), .in_0(d_ff_24_q), .in_1({6{1'b0}}), .out(Balance));
  Div #(.Bits(6)) C20 (.a(d_ff_24_q), .b(6'b010100), .q(C20_q), .r(C20_r));
  Div #(.Bits(6)) C10 (.a(C20_r), .b(6'b001010), .q(C10_q), .r(C10_r));
  Div #(.Bits(6)) C5 (.a(C10_r), .b(6'b000101), .q(C5_q));  // open: r
  Multiplexer #(.Bits(6)) multiplexer_5 (.sel(reset), .in_0(C20_q), .in_1({6{1'b0}}), .out(multiplexer_5_out));
  Multiplexer #(.Bits(6)) multiplexer_6 (.sel(reset), .in_0(C10_q), .in_1({6{1'b0}}), .out(multiplexer_6_out));
  Multiplexer #(.Bits(6)) multiplexer_7 (.sel(reset), .in_0(C5_q), .in_1({6{1'b0}}), .out(multiplexer_7_out));
  D_FF #(.Bits(6)) d_ff_25 (.D(multiplexer_5_out), .C(or_3_out), .Q({d_ff_25_q, Change20}));  // open: nQ
  D_FF #(.Bits(6)) d_ff_26 (.D(multiplexer_6_out), .C(or_3_out), .Q({d_ff_26_q, Change10}));  // open: nQ
  D_FF #(.Bits(6)) d_ff_27 (.D(multiplexer_7_out), .C(or_3_out), .Q({d_ff_27_q, Change5}));  // open: nQ

  // Notes on the sheet:
  //   INPUT
  //   OUTPUT
  //   ADD BALANCE
  //   BUY DRINK
  //   CALCULATE
  //   NEXT DRINK
  //   MONEY CHANGE
endmodule
