// Digital circuit diglab_10_01_template.dig as structural Verilog
module diglab_10_01_template (
  input  [8:0] N,
  input  reset,
  input  start,
  input  clock,
  output done,
  output [7:0] displayout,
  output [15:0] clockcount,
  output valid
);

  ROM #(.AddrBits(9), .Bits(8)) ROMFILE ();  // open: A, sel, D
  Seven_Seg_Hex seven_seg_hex_1 (.d(displayout[7:4]), .dp(1'b0));
  RAMDualPort #(.AddrBits(9), .Bits(8)) RAM ();  // open: A, Din, str, C, ld, D
  Seven_Seg_Hex seven_seg_hex_2 (.d(displayout[3:0]), .dp(1'b0));
endmodule
