// Digital circuit Midterm01_07.dig as structural Verilog
module Midterm01_07 (
  input  A2,
  input  A1,
  input  A0,
  input  B2,
  input  B1,
  input  B0,
  output Output
);

  wire add_1_c_o;

  Add #(.Bits(3)) add_1 (.a({B2, B1, B0}), .b({A2, A1, A0}), .c_i(1'b0), .c_o(add_1_c_o));  // open: s
  not not_1 (Output, add_1_c_o);
  Seven_Seg seven_seg_1 (.a(Output), .b(1'b1), .c(1'b1), .d(Output), .e(Output), .f(Output), .g(1'b0), .dp(1'b0));
endmodule
